// Digital circuit P01.dig as structural Verilog
module P01 (
  input  [7:0] M,
  input  [7:0] N,
  input  [13:0] progIn,
  input  reset,
  input  progLoad,
  input  start,
  input  result,
  input  clk,
  output valid,
  output done,
  output [7:0] \output 
);

  wire A_WE, A_we_t, B_sel, B_WE, B_we_t, BR, C_sel, C_we, CNT15, CNT_CLR, CNT_inc, CNT_WE, COND, JT, LDACC,
       PC_WE, RESOK, RS;
  wire [1:0] CS;
  wire [3:0] A_sel, ALU_F, CNT, CNT1, CNTD, NS, NS0, NS1, NS2, NS3;
  wire [7:0] ACCA, ACCB, AD, ALU, ALU_ADD, AMUX, BD, BMUX, IR, PA, PA1, PC, PCN, PCN0, RA, RDIN;
  wire [9:4] CADDR;
  wire [13:0] PD;
  wire [47:9] CW;

  Register #(.Bits(4)) STATE (.D(NS), .C(clk), .en(1'b1), .Q(CADDR[9:6]));
  ROM #(.AddrBits(10), .Bits(48)) ControlROM (
    .A({CADDR, ALU_F}), .sel(1'b1),
    .D({CW[47:35], CS, done, valid, CW[30:29], CNT_inc, CW[27:25], BR, CW[23:9], C_we, C_sel, B_we_t, B_sel, A_we_t, A_sel}));
  Seven_Seg_Hex seven_seg_hex_1 (.d(\output [7:4]), .dp(1'b0));
  Seven_Seg_Hex seven_seg_hex_2 (.d(\output [3:0]), .dp(1'b0));
  Multiplexer #(.Selector_Bits(2), .Bits(1)) multiplexer_1 (
    .sel(CS), .in_0(1'b0), .in_1(CNT15), .in_2(1'b0), .in_3(1'b0), .out(COND));
  Multiplexer #(.Selector_Bits(1), .Bits(4)) multiplexer_2 (.sel(COND), .in_0(CW[38:35]), .in_1(CW[42:39]), .out(NS0));
  and and_1 (RESOK, result, CW[30]);
  and and_2 (LDACC, progLoad, CW[29]);
  Multiplexer #(.Selector_Bits(1), .Bits(4)) multiplexer_3 (.sel(RESOK), .in_0(NS0), .in_1(4'b1010), .out(NS1));
  Multiplexer #(.Selector_Bits(1), .Bits(4)) multiplexer_4 (.sel(LDACC), .in_0(NS1), .in_1(4'b0001), .out(NS2));
  Multiplexer #(.Selector_Bits(1), .Bits(4)) multiplexer_5 (.sel(start), .in_0(NS2), .in_1(4'b0011), .out(NS3));
  Multiplexer #(.Selector_Bits(1), .Bits(4)) multiplexer_6 (.sel(reset), .in_0(NS3), .in_1(4'b0010), .out(NS));
  or or_1 (RS, reset, start);
  Multiplexer #(.Selector_Bits(2), .Bits(8)) multiplexer_7 (
    .sel(CW[15:14]), .in_0(PC), .in_1(IR), .in_2({8{1'b0}}), .in_3({8{1'b0}}), .out(PA));
  Add #(.Bits(8)) add_1 (.a(PA), .b(8'h1), .c_i(1'b0), .s(PA1));  // open: c_o
  Multiplexer #(.Selector_Bits(1), .Bits(8)) multiplexer_8 (.sel(JT), .in_0(PA1), .in_1(IR), .out(PCN0));
  Multiplexer #(.Selector_Bits(1), .Bits(8)) multiplexer_9 (.sel(RS), .in_0(PCN0), .in_1({8{1'b0}}), .out(PCN));
  or or_2 (PC_WE, RS, CW[22], LDACC, JT);
  Register #(.Bits(8)) u_PC (.D(PCN), .C(clk), .en(PC_WE), .Q(PC));
  RAMDualPort #(.AddrBits(8), .Bits(14)) pRAM (.A(PA), .Din(progIn), .str(LDACC), .C(clk), .ld(1'b1), .D(PD));
  Register #(.Bits(14)) u_IR (.D(PD), .C(clk), .en(CW[23]), .Q({CADDR[5:4], ALU_F, IR}));
  and and_3 (JT, BR, 1'b0);
  Multiplexer #(.Selector_Bits(4), .Bits(8)) multiplexer_10 (
    .sel(A_sel), .in_0(IR), .in_1(ACCB), .in_2({8{1'b0}}), .in_3({8{1'b0}}), .in_4({8{1'b0}}),
    .in_5(\output ), .in_6(PD[7:0]), .in_7(ALU), .in_8({8{1'b0}}), .in_9({8{1'b0}}), .in_10({8{1'b0}}),
    .in_11({8{1'b0}}), .in_12({8{1'b0}}), .in_13({8{1'b0}}), .in_14({8{1'b0}}), .in_15({8{1'b0}}), .out(AMUX));
  Multiplexer #(.Selector_Bits(1), .Bits(8)) multiplexer_11 (.sel(reset), .in_0(AMUX), .in_1({8{1'b0}}), .out(AD));
  or or_3 (A_WE, reset, A_we_t);
  Register #(.Bits(8)) u_accA (.D(AD), .C(clk), .en(A_WE), .Q(ACCA));
  Multiplexer #(.Selector_Bits(1), .Bits(8)) multiplexer_12 (.sel(B_sel), .in_0(IR), .in_1(ACCA), .out(BMUX));
  Multiplexer #(.Selector_Bits(1), .Bits(8)) multiplexer_13 (.sel(reset), .in_0(BMUX), .in_1({8{1'b0}}), .out(BD));
  or or_4 (B_WE, reset, B_we_t);
  Register #(.Bits(8)) u_accB (.D(BD), .C(clk), .en(B_WE), .Q(ACCB));
  Add #(.Bits(8)) add_2 (.a(ACCA), .b(ACCB), .c_i(1'b0), .s(ALU_ADD));  // open: c_o
  Multiplexer #(.Selector_Bits(4), .Bits(8)) multiplexer_14 (
    .sel(ALU_F), .in_0(ALU_ADD), .in_1({8{1'b0}}), .in_2({8{1'b0}}), .in_3({8{1'b0}}), .in_4({8{1'b0}}),
    .in_5({8{1'b0}}), .in_6({8{1'b0}}), .in_7({8{1'b0}}), .in_8({8{1'b0}}), .in_9({8{1'b0}}),
    .in_10({8{1'b0}}), .in_11({8{1'b0}}), .in_12({8{1'b0}}), .in_13({8{1'b0}}), .in_14({8{1'b0}}),
    .in_15({8{1'b0}}), .out(ALU));
  Multiplexer #(.Selector_Bits(3), .Bits(8)) multiplexer_15 (
    .sel(CW[18:16]), .in_0(IR), .in_1({8{1'b0}}), .in_2({8{1'b0}}), .in_3({8{1'b0}}), .in_4({4'b0000, CNT}),
    .in_5(8'ha), .in_6(8'hb), .in_7({8{1'b0}}), .out(RA));
  Multiplexer #(.Selector_Bits(2), .Bits(8)) multiplexer_16 (
    .sel(CW[21:20]), .in_0(ACCA), .in_1({8{1'b0}}), .in_2({8{1'b0}}), .in_3({8{1'b0}}), .out(RDIN));
  RAMDualPort #(.AddrBits(8), .Bits(8)) rRAM (.A(RA), .Din(RDIN), .str(CW[19]), .C(clk), .ld(1'b1), .D(\output ));
  Add #(.Bits(4)) add_3 (.a(CNT), .b(4'b0001), .c_i(1'b0), .s(CNT1), .c_o(CNT15));
  or or_5 (CNT_CLR, reset, RESOK);
  Multiplexer #(.Selector_Bits(1), .Bits(4)) multiplexer_17 (.sel(CNT_CLR), .in_0(CNT1), .in_1(4'b0000), .out(CNTD));
  or or_6 (CNT_WE, CNT_CLR, CNT_inc);
  Register #(.Bits(4)) u_CNT (.D(CNTD), .C(clk), .en(CNT_WE), .Q(CNT));

  // Other names for the same wires on the sheet: CNT8[3:0] = CNT;
  //   CW (some bits) = {CS, done, valid, CNT_inc, BR, C_we, C_sel, B_we_t, B_sel, A_we_t, A_sel};
  //   D_sel[1:0] = CW[10:9]; D_we = CW[11]; SP_op[1:0] = CW[13:12]; PA_sel[1:0] = CW[15:14]; RA_sel[2:0] = CW[18:16];
  //   R_we = CW[19]; RD_sel[1:0] = CW[21:20]; PC_inc = CW[22]; IR_we = CW[23]; DJNZ = CW[25]; F_cmp = CW[26];
  //   F_prime = CW[27]; W = CW[29]; RW = CW[30]; NSF[3:0] = CW[38:35]; NST[3:0] = CW[42:39]; OPR[7:0] = IR;
  //   CADDR[3:0] = ALU_F; IR[13:8] = {CADDR[5:4], ALU_F}; OP[5:0] = {CADDR[5:4], ALU_F}; OP_GRP[1:0] = CADDR[5:4];
  //   PD8[7:0] = PD[7:0]; RD[7:0] = \output ; STATE[3:0] = CADDR[9:6]

  // Notes on the sheet:
  //   Control ROM address = (STATE, OP)
  //   Control word bits:
  //   [0..3] A_sel
  //   [4] A_we
  //   [5] B_sel
  //   [6] B_we
  //   [7] C_sel
  //   [8] C_we
  //   [9..10] D_sel
  //   [11] D_we
  //   [12..13] SP_op
  //   [14..15] PA_sel
  //   [16..18] RA_sel
  //   [19] R_we
  //   [20..21] RD_sel
  //   [22] PC_inc
  //   [23] IR_we
  //   [24] BR
  //   [25] DJNZ
  //   [26] F_cmp
  //   [27] F_prime
  //   [28] CNT_inc
  //   [29] W
  //   [30] RW
  //   [31] valid
  //   [32] done
  //   [33..34] CS
  //   [35..38] NSF
  //   [39..42] NST
  //   [43..47] spare
  //   STATE encoding:
  //    0 = IDLE
  //    1 = LOAD
  //    2 = CLR
  //    3 = FETCH
  //    4 = EXEC
  //    5 = GCD
  //    6 = FIB
  //    7 = FIBH
  //    8 = FIBL
  //    9 = HALT
  //   10 = SEND
  //   11 = DONE
  //   CONTROL UNIT (state register + control ROM)
  //   contents of ControlROM (hex, n*v repeats v):
  //   64*20008000,64*20000000,64*12101c0000,64*22000c00000,19800000000
  //   ,19800000010,19800000040,14*19800000000,19800080000,14*19800000000
  //   ,19800000017,30*19800000000,4c800000000,256*0,64*4c8e0008000,64*5d290040000
  //   ,64*5d9e0008000
  //   NEXT-STATE LOGIC
  //   PC / pRAM / IR
  //   REGISTERS
  //   ALU
  //   rRAM / OUTPUT
endmodule

/* Test case 12_P12T01:
M N progIn reset progLoad start result clk valid done output
0 0 0 0 0 0 0 0 x x x
0 0 0 0 0 0 0 1 x x x
0 0 0 1 0 0 0 0 x x x
0 0 0 1 0 0 0 1 0 0 x
0 0 0 0 0 0 0 0 0 x x
0 0 0 0 0 0 0 1 0 x x
0 0 0 0 0 0 0 0 0 x x
0 0 0 0 0 0 0 1 0 x x
0 0 0 0 0 0 0 0 0 x x
0 0 0 0 0 0 0 1 0 x x
0 0 0 0 0 0 0 0 0 x x
0 0 0 0 0 0 0 1 0 x x
0 0 0 0 0 0 0 0 0 x x
0 0 0 0 0 0 0 1 0 x x
0 0 0 0 0 0 0 0 0 x x
0 0 0 0 0 0 0 1 0 x x
0 0 0 0 0 0 0 0 0 x x
0 0 0 0 0 0 0 1 0 x x
0 0 0 0 0 0 0 0 0 x x
0 0 0 0 0 0 0 1 0 x x
0 0 0 0 0 0 0 0 0 x x
0 0 0 0 0 0 0 1 0 x x
0 0 0 0 0 0 0 0 0 x x
0 0 0 0 0 0 0 1 0 x x
0 0 0 0 0 0 0 0 0 x x
0 0 0 0 0 0 0 1 0 x x
0 0 0 0 0 0 0 0 0 x x
0 0 0 0 0 0 0 1 0 x x
0 0 0 0 0 0 0 0 0 x x
0 0 0 0 0 0 0 1 0 x x
0 0 0 0 0 0 0 0 0 x x
0 0 0 0 0 0 0 1 0 x x
0 0 0 0 0 0 0 0 0 x x
0 0 0 0 0 0 0 1 0 x x
0 0 0 0 0 0 0 0 0 x x
0 0 0 0 0 0 0 1 0 x x
0 0 0 0 0 0 0 0 0 x x
0 0 0 0 0 0 0 1 0 x x
0 0 0 0 0 0 0 0 0 x x
0 0 0 0 0 0 0 1 0 x x
0 0 0 0 0 0 0 0 0 x x
0 0 0 0 0 0 0 1 0 x x
0 0 0 0 0 0 0 0 0 x x
0 0 0 0 0 0 0 1 0 x x
0 0 268 0 1 0 0 0 0 x x
0 0 268 0 1 0 0 1 0 x x
0 0 530 0 1 0 0 0 0 x x
0 0 530 0 1 0 0 1 0 x x
0 0 15360 0 1 0 0 0 0 x x
0 0 15360 0 1 0 0 1 0 x x
0 0 4352 0 1 0 0 0 0 x x
0 0 4352 0 1 0 0 1 0 x x
0 0 356 0 1 0 0 0 0 x x
0 0 356 0 1 0 0 1 0 x x
0 0 587 0 1 0 0 0 0 x x
0 0 587 0 1 0 0 1 0 x x
0 0 15360 0 1 0 0 0 0 x x
0 0 15360 0 1 0 0 1 0 x x
0 0 4353 0 1 0 0 0 0 x x
0 0 4353 0 1 0 0 1 0 x x
0 0 273 0 1 0 0 0 0 x x
0 0 273 0 1 0 0 1 0 x x
0 0 517 0 1 0 0 0 0 x x
0 0 517 0 1 0 0 1 0 x x
0 0 15360 0 1 0 0 0 0 x x
0 0 15360 0 1 0 0 1 0 x x
0 0 4354 0 1 0 0 0 0 x x
0 0 4354 0 1 0 0 1 0 x x
0 0 304 0 1 0 0 0 0 x x
0 0 304 0 1 0 0 1 0 x x
0 0 560 0 1 0 0 0 0 x x
0 0 560 0 1 0 0 1 0 x x
0 0 15360 0 1 0 0 0 0 x x
0 0 15360 0 1 0 0 1 0 x x
0 0 4355 0 1 0 0 0 0 x x
0 0 4355 0 1 0 0 1 0 x x
0 0 1024 0 1 0 0 0 0 x x
0 0 1024 0 1 0 0 1 0 x x
0 0 4367 0 1 0 0 0 0 x x
0 0 4367 0 1 0 0 1 0 x x
0 0 16128 0 1 0 0 0 0 x x
0 0 16128 0 1 0 0 1 0 x x
0 0 0 0 0 1 0 0 x x x
0 0 0 0 0 1 0 1 x 0 x
0 0 0 0 0 0 0 0 x 0 x
0 0 0 0 0 0 0 1 x 0 x
0 0 0 0 0 0 0 0 x 0 x
0 0 0 0 0 0 0 1 x 0 x
0 0 0 0 0 0 0 0 x 0 x
0 0 0 0 0 0 0 1 x 0 x
0 0 0 0 0 0 0 0 x 0 x
0 0 0 0 0 0 0 1 x 0 x
0 0 0 0 0 0 0 0 x 0 x
0 0 0 0 0 0 0 1 x 0 x
0 0 0 0 0 0 0 0 x 0 x
0 0 0 0 0 0 0 1 x 0 x
0 0 0 0 0 0 0 0 x 0 x
0 0 0 0 0 0 0 1 x 0 x
0 0 0 0 0 0 0 0 x 0 x
0 0 0 0 0 0 0 1 x 0 x
0 0 0 0 0 0 0 0 x 0 x
0 0 0 0 0 0 0 1 x 0 x
0 0 0 0 0 0 0 0 x 0 x
0 0 0 0 0 0 0 1 x 0 x
0 0 0 0 0 0 0 0 x 0 x
0 0 0 0 0 0 0 1 x 0 x
0 0 0 0 0 0 0 0 x 0 x
0 0 0 0 0 0 0 1 x 0 x
0 0 0 0 0 0 0 0 x 0 x
0 0 0 0 0 0 0 1 x 0 x
0 0 0 0 0 0 0 0 x 0 x
0 0 0 0 0 0 0 1 x 0 x
0 0 0 0 0 0 0 0 x 0 x
0 0 0 0 0 0 0 1 x 0 x
0 0 0 0 0 0 0 0 x 0 x
0 0 0 0 0 0 0 1 x 0 x
0 0 0 0 0 0 0 0 x 0 x
0 0 0 0 0 0 0 1 x 0 x
0 0 0 0 0 0 0 0 x 0 x
0 0 0 0 0 0 0 1 x 0 x
0 0 0 0 0 0 0 0 x 0 x
0 0 0 0 0 0 0 1 x 0 x
0 0 0 0 0 0 0 0 x 0 x
0 0 0 0 0 0 0 1 x 0 x
0 0 0 0 0 0 0 0 x 0 x
0 0 0 0 0 0 0 1 x 0 x
0 0 0 0 0 0 0 0 x 0 x
0 0 0 0 0 0 0 1 x 0 x
0 0 0 0 0 0 0 0 x 0 x
0 0 0 0 0 0 0 1 x 0 x
0 0 0 0 0 0 0 0 x 0 x
0 0 0 0 0 0 0 1 x 0 x
0 0 0 0 0 0 0 0 x 0 x
0 0 0 0 0 0 0 1 x 0 x
0 0 0 0 0 0 0 0 x 0 x
0 0 0 0 0 0 0 1 x 0 x
0 0 0 0 0 0 0 0 x 0 x
0 0 0 0 0 0 0 1 x 0 x
0 0 0 0 0 0 0 0 x 0 x
0 0 0 0 0 0 0 1 x 0 x
0 0 0 0 0 0 0 0 x 0 x
0 0 0 0 0 0 0 1 x 0 x
0 0 0 0 0 0 0 0 x 0 x
0 0 0 0 0 0 0 1 x 0 x
0 0 0 0 0 0 0 0 x 0 x
0 0 0 0 0 0 0 1 x 0 x
0 0 0 0 0 0 0 0 x 0 x
0 0 0 0 0 0 0 1 x 0 x
0 0 0 0 0 0 0 0 x 0 x
0 0 0 0 0 0 0 1 x 0 x
0 0 0 0 0 0 0 0 x 0 x
0 0 0 0 0 0 0 1 x 0 x
0 0 0 0 0 0 0 0 x 0 x
0 0 0 0 0 0 0 1 x 0 x
0 0 0 0 0 0 0 0 x 0 x
0 0 0 0 0 0 0 1 x 0 x
0 0 0 0 0 0 0 0 x 0 x
0 0 0 0 0 0 0 1 x 0 x
0 0 0 0 0 0 0 0 x 0 x
0 0 0 0 0 0 0 1 x 0 x
0 0 0 0 0 0 0 0 x 0 x
0 0 0 0 0 0 0 1 x 0 x
0 0 0 0 0 0 0 0 x 0 x
0 0 0 0 0 0 0 1 x 0 x
0 0 0 0 0 0 0 0 x 0 x
0 0 0 0 0 0 0 1 x 0 x
0 0 0 0 0 0 0 0 x 0 x
0 0 0 0 0 0 0 1 x 0 x
0 0 0 0 0 0 0 0 x 0 x
0 0 0 0 0 0 0 1 x 0 x
0 0 0 0 0 0 0 0 x 0 x
0 0 0 0 0 0 0 1 x 0 x
0 0 0 0 0 0 0 0 x 0 x
0 0 0 0 0 0 0 1 x 0 x
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*/

/* Test case 06_P06T01:
M N progIn reset progLoad start result clk valid done output
0 0 0 0 0 0 0 0 x x x
0 0 0 0 0 0 0 1 x x x
0 0 0 1 0 0 0 0 x x x
0 0 0 1 0 0 0 1 0 0 x
0 0 0 0 0 0 0 0 0 x x
0 0 0 0 0 0 0 1 0 x x
0 0 0 0 0 0 0 0 0 x x
0 0 0 0 0 0 0 1 0 x x
0 0 0 0 0 0 0 0 0 x x
0 0 0 0 0 0 0 1 0 x x
0 0 0 0 0 0 0 0 0 x x
0 0 0 0 0 0 0 1 0 x x
0 0 0 0 0 0 0 0 0 x x
0 0 0 0 0 0 0 1 0 x x
0 0 0 0 0 0 0 0 0 x x
0 0 0 0 0 0 0 1 0 x x
0 0 0 0 0 0 0 0 0 x x
0 0 0 0 0 0 0 1 0 x x
0 0 0 0 0 0 0 0 0 x x
0 0 0 0 0 0 0 1 0 x x
0 0 0 0 0 0 0 0 0 x x
0 0 0 0 0 0 0 1 0 x x
0 0 0 0 0 0 0 0 0 x x
0 0 0 0 0 0 0 1 0 x x
0 0 0 0 0 0 0 0 0 x x
0 0 0 0 0 0 0 1 0 x x
0 0 0 0 0 0 0 0 0 x x
0 0 0 0 0 0 0 1 0 x x
0 0 0 0 0 0 0 0 0 x x
0 0 0 0 0 0 0 1 0 x x
0 0 0 0 0 0 0 0 0 x x
0 0 0 0 0 0 0 1 0 x x
0 0 0 0 0 0 0 0 0 x x
0 0 0 0 0 0 0 1 0 x x
0 0 0 0 0 0 0 0 0 x x
0 0 0 0 0 0 0 1 0 x x
0 0 0 0 0 0 0 0 0 x x
0 0 0 0 0 0 0 1 0 x x
0 0 0 0 0 0 0 0 0 x x
0 0 0 0 0 0 0 1 0 x x
0 0 0 0 0 0 0 0 0 x x
0 0 0 0 0 0 0 1 0 x x
0 0 0 0 0 0 0 0 0 x x
0 0 0 0 0 0 0 1 0 x x
0 0 3072 0 1 0 0 0 0 x x
0 0 3072 0 1 0 0 1 0 x x
0 0 3328 0 1 0 0 0 0 x x
0 0 3328 0 1 0 0 1 0 x x
0 0 2048 0 1 0 0 0 0 x x
0 0 2048 0 1 0 0 1 0 x x
0 0 4352 0 1 0 0 0 0 x x
0 0 4352 0 1 0 0 1 0 x x
0 0 2304 0 1 0 0 0 0 x x
0 0 2304 0 1 0 0 1 0 x x
0 0 4353 0 1 0 0 0 0 x x
0 0 4353 0 1 0 0 1 0 x x
0 0 2048 0 1 0 0 0 0 x x
0 0 2048 0 1 0 0 1 0 x x
0 0 1280 0 1 0 0 0 0 x x
0 0 1280 0 1 0 0 1 0 x x
0 0 2304 0 1 0 0 0 0 x x
0 0 2304 0 1 0 0 1 0 x x
0 0 8192 0 1 0 0 0 0 x x
0 0 8192 0 1 0 0 1 0 x x
0 0 4354 0 1 0 0 0 0 x x
0 0 4354 0 1 0 0 1 0 x x
0 0 16128 0 1 0 0 0 0 x x
0 0 16128 0 1 0 0 1 0 x x
18 52 0 0 0 1 0 0 x x x
18 52 0 0 0 1 0 1 x 0 x
18 52 0 0 0 0 0 0 x 0 x
18 52 0 0 0 0 0 1 x 0 x
18 52 0 0 0 0 0 0 x 0 x
18 52 0 0 0 0 0 1 x 0 x
18 52 0 0 0 0 0 0 x 0 x
18 52 0 0 0 0 0 1 x 0 x
18 52 0 0 0 0 0 0 x 0 x
18 52 0 0 0 0 0 1 x 0 x
18 52 0 0 0 0 0 0 x 0 x
18 52 0 0 0 0 0 1 x 0 x
18 52 0 0 0 0 0 0 x 0 x
18 52 0 0 0 0 0 1 x 0 x
18 52 0 0 0 0 0 0 x 0 x
18 52 0 0 0 0 0 1 x 0 x
18 52 0 0 0 0 0 0 x 0 x
18 52 0 0 0 0 0 1 x 0 x
18 52 0 0 0 0 0 0 x 0 x
18 52 0 0 0 0 0 1 x 0 x
18 52 0 0 0 0 0 0 x 0 x
18 52 0 0 0 0 0 1 x 0 x
18 52 0 0 0 0 0 0 x 0 x
18 52 0 0 0 0 0 1 x 0 x
18 52 0 0 0 0 0 0 x 0 x
18 52 0 0 0 0 0 1 x 0 x
18 52 0 0 0 0 0 0 x 0 x
18 52 0 0 0 0 0 1 x 0 x
18 52 0 0 0 0 0 0 x 0 x
18 52 0 0 0 0 0 1 x 0 x
18 52 0 0 0 0 0 0 x 0 x
18 52 0 0 0 0 0 1 x 0 x
18 52 0 0 0 0 0 0 x 0 x
18 52 0 0 0 0 0 1 x 0 x
18 52 0 0 0 0 0 0 x 0 x
18 52 0 0 0 0 0 1 x 0 x
18 52 0 0 0 0 0 0 x 0 x
18 52 0 0 0 0 0 1 x 0 x
18 52 0 0 0 0 0 0 x 0 x
18 52 0 0 0 0 0 1 x 0 x
18 52 0 0 0 0 0 0 x 0 x
18 52 0 0 0 0 0 1 x 0 x
18 52 0 0 0 0 0 0 x 0 x
18 52 0 0 0 0 0 1 x 0 x
18 52 0 0 0 0 0 0 x 0 x
18 52 0 0 0 0 0 1 x 0 x
18 52 0 0 0 0 0 0 x 0 x
18 52 0 0 0 0 0 1 x 0 x
18 52 0 0 0 0 0 0 x 0 x
18 52 0 0 0 0 0 1 x 0 x
18 52 0 0 0 0 0 0 x 0 x
18 52 0 0 0 0 0 1 x 0 x
18 52 0 0 0 0 0 0 x 0 x
18 52 0 0 0 0 0 1 x 0 x
18 52 0 0 0 0 0 0 x 0 x
18 52 0 0 0 0 0 1 x 0 x
18 52 0 0 0 0 0 0 x 0 x
18 52 0 0 0 0 0 1 x 0 x
18 52 0 0 0 0 0 0 x 0 x
18 52 0 0 0 0 0 1 x 0 x
18 52 0 0 0 0 0 0 x 0 x
18 52 0 0 0 0 0 1 x 0 x
18 52 0 0 0 0 0 0 x 0 x
18 52 0 0 0 0 0 1 x 0 x
18 52 0 0 0 0 0 0 x 0 x
18 52 0 0 0 0 0 1 x 0 x
18 52 0 0 0 0 0 0 x 0 x
18 52 0 0 0 0 0 1 x 0 x
18 52 0 0 0 0 0 0 x 0 x
18 52 0 0 0 0 0 1 x 0 x
18 52 0 0 0 0 0 0 x 0 x
18 52 0 0 0 0 0 1 x 0 x
18 52 0 0 0 0 0 0 x 0 x
18 52 0 0 0 0 0 1 x 0 x
18 52 0 0 0 0 0 0 x 0 x
18 52 0 0 0 0 0 1 x 0 x
18 52 0 0 0 0 0 0 x 0 x
18 52 0 0 0 0 0 1 x 0 x
18 52 0 0 0 0 0 0 x 0 x
18 52 0 0 0 0 0 1 x 0 x
18 52 0 0 0 0 0 0 x 0 x
18 52 0 0 0 0 0 1 x 0 x
18 52 0 0 0 0 0 0 x 0 x
18 52 0 0 0 0 0 1 x 0 x
18 52 0 0 0 0 0 0 x 0 x
18 52 0 0 0 0 0 1 x 0 x
18 52 0 0 0 0 0 0 x 0 x
18 52 0 0 0 0 0 1 x 0 x
18 52 0 0 0 0 0 0 x 0 x
18 52 0 0 0 0 0 1 x 0 x
18 52 0 0 0 0 0 0 x 0 x
18 52 0 0 0 0 0 1 x 0 x
18 52 0 0 0 0 0 0 x 0 x
18 52 0 0 0 0 0 1 x 0 x
18 52 0 0 0 0 0 0 x 0 x
18 52 0 0 0 0 0 1 x 0 x
18 52 0 0 0 0 0 0 x 0 x
18 52 0 0 0 0 0 1 x 0 x
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*/

/* Test case 11_P11T01:
M N progIn reset progLoad start result clk valid done output
0 0 0 0 0 0 0 0 x x x
0 0 0 0 0 0 0 1 x x x
0 0 0 1 0 0 0 0 x x x
0 0 0 1 0 0 0 1 0 0 x
0 0 0 0 0 0 0 0 0 x x
0 0 0 0 0 0 0 1 0 x x
0 0 0 0 0 0 0 0 0 x x
0 0 0 0 0 0 0 1 0 x x
0 0 0 0 0 0 0 0 0 x x
0 0 0 0 0 0 0 1 0 x x
0 0 0 0 0 0 0 0 0 x x
0 0 0 0 0 0 0 1 0 x x
0 0 0 0 0 0 0 0 0 x x
0 0 0 0 0 0 0 1 0 x x
0 0 0 0 0 0 0 0 0 x x
0 0 0 0 0 0 0 1 0 x x
0 0 0 0 0 0 0 0 0 x x
0 0 0 0 0 0 0 1 0 x x
0 0 0 0 0 0 0 0 0 x x
0 0 0 0 0 0 0 1 0 x x
0 0 0 0 0 0 0 0 0 x x
0 0 0 0 0 0 0 1 0 x x
0 0 0 0 0 0 0 0 0 x x
0 0 0 0 0 0 0 1 0 x x
0 0 0 0 0 0 0 0 0 x x
0 0 0 0 0 0 0 1 0 x x
0 0 0 0 0 0 0 0 0 x x
0 0 0 0 0 0 0 1 0 x x
0 0 0 0 0 0 0 0 0 x x
0 0 0 0 0 0 0 1 0 x x
0 0 0 0 0 0 0 0 0 x x
0 0 0 0 0 0 0 1 0 x x
0 0 0 0 0 0 0 0 0 x x
0 0 0 0 0 0 0 1 0 x x
0 0 0 0 0 0 0 0 0 x x
0 0 0 0 0 0 0 1 0 x x
0 0 0 0 0 0 0 0 0 x x
0 0 0 0 0 0 0 1 0 x x
0 0 0 0 0 0 0 0 0 x x
0 0 0 0 0 0 0 1 0 x x
0 0 0 0 0 0 0 0 0 x x
0 0 0 0 0 0 0 1 0 x x
0 0 0 0 0 0 0 0 0 x x
0 0 0 0 0 0 0 1 0 x x
0 0 3328 0 1 0 0 0 0 x x
0 0 3328 0 1 0 0 1 0 x x
0 0 256 0 1 0 0 0 0 x x
0 0 256 0 1 0 0 1 0 x x
0 0 1280 0 1 0 0 0 0 x x
0 0 1280 0 1 0 0 1 0 x x
0 0 2304 0 1 0 0 0 0 x x
0 0 2304 0 1 0 0 1 0 x x
0 0 8192 0 1 0 0 0 0 x x
0 0 8192 0 1 0 0 1 0 x x
0 0 13314 0 1 0 0 0 0 x x
0 0 13314 0 1 0 0 1 0 x x
0 0 4352 0 1 0 0 0 0 x x
0 0 4352 0 1 0 0 1 0 x x
0 0 2304 0 1 0 0 0 0 x x
0 0 2304 0 1 0 0 1 0 x x
0 0 4353 0 1 0 0 0 0 x x
0 0 4353 0 1 0 0 1 0 x x
0 0 16128 0 1 0 0 0 0 x x
0 0 16128 0 1 0 0 1 0 x x
0 10 0 0 0 1 0 0 x x x
0 10 0 0 0 1 0 1 x 0 x
0 10 0 0 0 0 0 0 x 0 x
0 10 0 0 0 0 0 1 x 0 x
0 10 0 0 0 0 0 0 x 0 x
0 10 0 0 0 0 0 1 x 0 x
0 10 0 0 0 0 0 0 x 0 x
0 10 0 0 0 0 0 1 x 0 x
0 10 0 0 0 0 0 0 x 0 x
0 10 0 0 0 0 0 1 x 0 x
0 10 0 0 0 0 0 0 x 0 x
0 10 0 0 0 0 0 1 x 0 x
0 10 0 0 0 0 0 0 x 0 x
0 10 0 0 0 0 0 1 x 0 x
0 10 0 0 0 0 0 0 x 0 x
0 10 0 0 0 0 0 1 x 0 x
0 10 0 0 0 0 0 0 x 0 x
0 10 0 0 0 0 0 1 x 0 x
0 10 0 0 0 0 0 0 x 0 x
0 10 0 0 0 0 0 1 x 0 x
0 10 0 0 0 0 0 0 x 0 x
0 10 0 0 0 0 0 1 x 0 x
0 10 0 0 0 0 0 0 x 0 x
0 10 0 0 0 0 0 1 x 0 x
0 10 0 0 0 0 0 0 x 0 x
0 10 0 0 0 0 0 1 x 0 x
0 10 0 0 0 0 0 0 x 0 x
0 10 0 0 0 0 0 1 x 0 x
0 10 0 0 0 0 0 0 x 0 x
0 10 0 0 0 0 0 1 x 0 x
0 10 0 0 0 0 0 0 x 0 x
0 10 0 0 0 0 0 1 x 0 x
0 10 0 0 0 0 0 0 x 0 x
0 10 0 0 0 0 0 1 x 0 x
0 10 0 0 0 0 0 0 x 0 x
0 10 0 0 0 0 0 1 x 0 x
0 10 0 0 0 0 0 0 x 0 x
0 10 0 0 0 0 0 1 x 0 x
0 10 0 0 0 0 0 0 x 0 x
0 10 0 0 0 0 0 1 x 0 x
0 10 0 0 0 0 0 0 x 0 x
0 10 0 0 0 0 0 1 x 0 x
0 10 0 0 0 0 0 0 x 0 x
0 10 0 0 0 0 0 1 x 0 x
0 10 0 0 0 0 0 0 x 0 x
0 10 0 0 0 0 0 1 x 0 x
0 10 0 0 0 0 0 0 x 0 x
0 10 0 0 0 0 0 1 x 0 x
0 10 0 0 0 0 0 0 x 0 x
0 10 0 0 0 0 0 1 x 0 x
0 10 0 0 0 0 0 0 x 0 x
0 10 0 0 0 0 0 1 x 0 x
0 10 0 0 0 0 0 0 x 0 x
0 10 0 0 0 0 0 1 x 0 x
0 10 0 0 0 0 0 0 x 0 x
0 10 0 0 0 0 0 1 x 0 x
0 10 0 0 0 0 0 0 x 0 x
0 10 0 0 0 0 0 1 x 0 x
0 10 0 0 0 0 0 0 x 0 x
0 10 0 0 0 0 0 1 x 0 x
0 10 0 0 0 0 0 0 x 0 x
0 10 0 0 0 0 0 1 x 0 x
0 10 0 0 0 0 0 0 x 0 x
0 10 0 0 0 0 0 1 x 0 x
0 10 0 0 0 0 0 0 x 0 x
0 10 0 0 0 0 0 1 x 0 x
0 10 0 0 0 0 0 0 x 0 x
0 10 0 0 0 0 0 1 x 0 x
0 10 0 0 0 0 0 0 x 0 x
0 10 0 0 0 0 0 1 x 0 x
0 10 0 0 0 0 0 0 x 0 x
0 10 0 0 0 0 0 1 x 0 x
0 10 0 0 0 0 0 0 x 0 x
0 10 0 0 0 0 0 1 x 0 x
0 10 0 0 0 0 0 0 x 0 x
0 10 0 0 0 0 0 1 x 0 x
0 10 0 0 0 0 0 0 x 0 x
0 10 0 0 0 0 0 1 x 0 x
0 10 0 0 0 0 0 0 x 0 x
0 10 0 0 0 0 0 1 x 0 x
0 10 0 0 0 0 0 0 x 0 x
0 10 0 0 0 0 0 1 x 0 x
0 10 0 0 0 0 0 0 x 0 x
0 10 0 0 0 0 0 1 x 0 x
0 10 0 0 0 0 0 0 x 0 x
0 10 0 0 0 0 0 1 x 0 x
0 10 0 0 0 0 0 0 x 0 x
0 10 0 0 0 0 0 1 x 0 x
0 10 0 0 0 0 0 0 x 0 x
0 10 0 0 0 0 0 1 x 0 x
0 10 0 0 0 0 0 0 x 0 x
0 10 0 0 0 0 0 1 x 0 x
0 10 0 0 0 0 0 0 x 0 x
0 10 0 0 0 0 0 1 x 0 x
0 10 0 0 0 0 0 0 x 0 x
0 10 0 0 0 0 0 1 x 0 x
0 10 0 0 0 0 0 0 x 0 x
0 10 0 0 0 0 0 1 x 0 x
0 10 0 0 0 0 0 0 x 0 x
0 10 0 0 0 0 0 1 x 0 x
0 10 0 0 0 0 0 0 x 0 x
0 10 0 0 0 0 0 1 x 0 x
0 10 0 0 0 0 0 0 x 0 x
0 10 0 0 0 0 0 1 x 0 x
0 10 0 0 0 0 0 0 x 0 x
0 10 0 0 0 0 0 1 x 0 x
0 10 0 0 0 0 0 0 x 0 x
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*/

/* Test case 05_P05T01:
M N progIn reset progLoad start result clk valid done output
0 0 0 0 0 0 0 0 x x x
0 0 0 0 0 0 0 1 x x x
0 0 0 1 0 0 0 0 x x x
0 0 0 1 0 0 0 1 0 0 x
0 0 0 0 0 0 0 0 0 x x
0 0 0 0 0 0 0 1 0 x x
0 0 0 0 0 0 0 0 0 x x
0 0 0 0 0 0 0 1 0 x x
0 0 0 0 0 0 0 0 0 x x
0 0 0 0 0 0 0 1 0 x x
0 0 0 0 0 0 0 0 0 x x
0 0 0 0 0 0 0 1 0 x x
0 0 0 0 0 0 0 0 0 x x
0 0 0 0 0 0 0 1 0 x x
0 0 0 0 0 0 0 0 0 x x
0 0 0 0 0 0 0 1 0 x x
0 0 0 0 0 0 0 0 0 x x
0 0 0 0 0 0 0 1 0 x x
0 0 0 0 0 0 0 0 0 x x
0 0 0 0 0 0 0 1 0 x x
0 0 0 0 0 0 0 0 0 x x
0 0 0 0 0 0 0 1 0 x x
0 0 0 0 0 0 0 0 0 x x
0 0 0 0 0 0 0 1 0 x x
0 0 0 0 0 0 0 0 0 x x
0 0 0 0 0 0 0 1 0 x x
0 0 0 0 0 0 0 0 0 x x
0 0 0 0 0 0 0 1 0 x x
0 0 0 0 0 0 0 0 0 x x
0 0 0 0 0 0 0 1 0 x x
0 0 0 0 0 0 0 0 0 x x
0 0 0 0 0 0 0 1 0 x x
0 0 0 0 0 0 0 0 0 x x
0 0 0 0 0 0 0 1 0 x x
0 0 0 0 0 0 0 0 0 x x
0 0 0 0 0 0 0 1 0 x x
0 0 0 0 0 0 0 0 0 x x
0 0 0 0 0 0 0 1 0 x x
0 0 0 0 0 0 0 0 0 x x
0 0 0 0 0 0 0 1 0 x x
0 0 0 0 0 0 0 0 0 x x
0 0 0 0 0 0 0 1 0 x x
0 0 0 0 0 0 0 0 0 x x
0 0 0 0 0 0 0 1 0 x x
0 0 265 0 1 0 0 0 0 x x
0 0 265 0 1 0 0 1 0 x x
0 0 515 0 1 0 0 0 0 x x
0 0 515 0 1 0 0 1 0 x x
0 0 14336 0 1 0 0 0 0 x x
0 0 14336 0 1 0 0 1 0 x x
0 0 14592 0 1 0 0 0 0 x x
0 0 14592 0 1 0 0 1 0 x x
0 0 12562 0 1 0 0 0 0 x x
0 0 12562 0 1 0 0 1 0 x x
0 0 12807 0 1 0 0 0 0 x x
0 0 12807 0 1 0 0 1 0 x x
0 0 12306 0 1 0 0 0 0 x x
0 0 12306 0 1 0 0 1 0 x x
0 0 257 0 1 0 0 0 0 x x
0 0 257 0 1 0 0 1 0 x x
0 0 4352 0 1 0 0 0 0 x x
0 0 4352 0 1 0 0 1 0 x x
0 0 267 0 1 0 0 0 0 x x
0 0 267 0 1 0 0 1 0 x x
0 0 14592 0 1 0 0 0 0 x x
0 0 14592 0 1 0 0 1 0 x x
0 0 12557 0 1 0 0 0 0 x x
0 0 12557 0 1 0 0 1 0 x x
0 0 12306 0 1 0 0 0 0 x x
0 0 12306 0 1 0 0 1 0 x x
0 0 12815 0 1 0 0 0 0 x x
0 0 12815 0 1 0 0 1 0 x x
0 0 12306 0 1 0 0 0 0 x x
0 0 12306 0 1 0 0 1 0 x x
0 0 258 0 1 0 0 0 0 x x
0 0 258 0 1 0 0 1 0 x x
0 0 4353 0 1 0 0 0 0 x x
0 0 4353 0 1 0 0 1 0 x x
0 0 16128 0 1 0 0 0 0 x x
0 0 16128 0 1 0 0 1 0 x x
0 0 494 0 1 0 0 0 0 x x
0 0 494 0 1 0 0 1 0 x x
0 0 4367 0 1 0 0 0 0 x x
0 0 4367 0 1 0 0 1 0 x x
0 0 16128 0 1 0 0 0 0 x x
0 0 16128 0 1 0 0 1 0 x x
0 0 0 0 0 1 0 0 x x x
0 0 0 0 0 1 0 1 x 0 x
0 0 0 0 0 0 0 0 x 0 x
0 0 0 0 0 0 0 1 x 0 x
0 0 0 0 0 0 0 0 x 0 x
0 0 0 0 0 0 0 1 x 0 x
0 0 0 0 0 0 0 0 x 0 x
0 0 0 0 0 0 0 1 x 0 x
0 0 0 0 0 0 0 0 x 0 x
0 0 0 0 0 0 0 1 x 0 x
0 0 0 0 0 0 0 0 x 0 x
0 0 0 0 0 0 0 1 x 0 x
0 0 0 0 0 0 0 0 x 0 x
0 0 0 0 0 0 0 1 x 0 x
0 0 0 0 0 0 0 0 x 0 x
0 0 0 0 0 0 0 1 x 0 x
0 0 0 0 0 0 0 0 x 0 x
0 0 0 0 0 0 0 1 x 0 x
0 0 0 0 0 0 0 0 x 0 x
0 0 0 0 0 0 0 1 x 0 x
0 0 0 0 0 0 0 0 x 0 x
0 0 0 0 0 0 0 1 x 0 x
0 0 0 0 0 0 0 0 x 0 x
0 0 0 0 0 0 0 1 x 0 x
0 0 0 0 0 0 0 0 x 0 x
0 0 0 0 0 0 0 1 x 0 x
0 0 0 0 0 0 0 0 x 0 x
0 0 0 0 0 0 0 1 x 0 x
0 0 0 0 0 0 0 0 x 0 x
0 0 0 0 0 0 0 1 x 0 x
0 0 0 0 0 0 0 0 x 0 x
0 0 0 0 0 0 0 1 x 0 x
0 0 0 0 0 0 0 0 x 0 x
0 0 0 0 0 0 0 1 x 0 x
0 0 0 0 0 0 0 0 x 0 x
0 0 0 0 0 0 0 1 x 0 x
0 0 0 0 0 0 0 0 x 0 x
0 0 0 0 0 0 0 1 x 0 x
0 0 0 0 0 0 0 0 x 0 x
0 0 0 0 0 0 0 1 x 0 x
0 0 0 0 0 0 0 0 x 0 x
0 0 0 0 0 0 0 1 x 0 x
0 0 0 0 0 0 0 0 x 0 x
0 0 0 0 0 0 0 1 x 0 x
0 0 0 0 0 0 0 0 x 0 x
0 0 0 0 0 0 0 1 x 0 x
0 0 0 0 0 0 0 0 x 0 x
0 0 0 0 0 0 0 1 x 0 x
0 0 0 0 0 0 0 0 x 0 x
0 0 0 0 0 0 0 1 x 0 x
0 0 0 0 0 0 0 0 x 0 x
0 0 0 0 0 0 0 1 x 0 x
0 0 0 0 0 0 0 0 x 0 x
0 0 0 0 0 0 0 1 x 0 x
0 0 0 0 0 0 0 0 x 0 x
0 0 0 0 0 0 0 1 x 0 x
0 0 0 0 0 0 0 0 x 0 x
0 0 0 0 0 0 0 1 x 0 x
0 0 0 0 0 0 0 0 x 0 x
0 0 0 0 0 0 0 1 x 0 x
0 0 0 0 0 0 0 0 x 0 x
0 0 0 0 0 0 0 1 x 0 x
0 0 0 0 0 0 0 0 x 0 x
0 0 0 0 0 0 0 1 x 0 x
0 0 0 0 0 0 0 0 x 0 x
0 0 0 0 0 0 0 1 x 0 x
0 0 0 0 0 0 0 0 x 0 x
0 0 0 0 0 0 0 1 x 0 x
0 0 0 0 0 0 0 0 x 0 x
0 0 0 0 0 0 0 1 x 0 x
0 0 0 0 0 0 0 0 x 0 x
0 0 0 0 0 0 0 1 x 0 x
0 0 0 0 0 0 0 0 x 0 x
0 0 0 0 0 0 0 1 x 0 x
0 0 0 0 0 0 0 0 x 0 x
0 0 0 0 0 0 0 1 x 0 x
0 0 0 0 0 0 0 0 x 0 x
0 0 0 0 0 0 0 1 x 0 x
0 0 0 0 0 0 0 0 x 0 x
0 0 0 0 0 0 0 1 x 0 x
0 0 0 0 0 0 0 0 x 0 x
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*/

/* Test case 10_P10T01:
M N progIn reset progLoad start result clk valid done output
0 0 0 0 0 0 0 0 x x x
0 0 0 0 0 0 0 1 x x x
0 0 0 1 0 0 0 0 x x x
0 0 0 1 0 0 0 1 0 0 x
0 0 0 0 0 0 0 0 0 x x
0 0 0 0 0 0 0 1 0 x x
0 0 0 0 0 0 0 0 0 x x
0 0 0 0 0 0 0 1 0 x x
0 0 0 0 0 0 0 0 0 x x
0 0 0 0 0 0 0 1 0 x x
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*/

/* Test case 04_P04T01:
M N progIn reset progLoad start result clk valid done output
0 0 0 0 0 0 0 0 x x x
0 0 0 0 0 0 0 1 x x x
0 0 0 1 0 0 0 0 x x x
0 0 0 1 0 0 0 1 0 0 x
0 0 0 0 0 0 0 0 0 x x
0 0 0 0 0 0 0 1 0 x x
0 0 0 0 0 0 0 0 0 x x
0 0 0 0 0 0 0 1 0 x x
0 0 0 0 0 0 0 0 0 x x
0 0 0 0 0 0 0 1 0 x x
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*/

/* Test case 09_P09T01:
M N progIn reset progLoad start result clk valid done output
0 0 0 0 0 0 0 0 x x x
0 0 0 0 0 0 0 1 x x x
0 0 0 1 0 0 0 0 x x x
0 0 0 1 0 0 0 1 0 0 x
0 0 0 0 0 0 0 0 0 x x
0 0 0 0 0 0 0 1 0 x x
0 0 0 0 0 0 0 0 0 x x
0 0 0 0 0 0 0 1 0 x x
0 0 0 0 0 0 0 0 0 x x
0 0 0 0 0 0 0 1 0 x x
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*/

/* Test case 03_P03T01:
M N progIn reset progLoad start result clk valid done output
0 0 0 0 0 0 0 0 x x x
0 0 0 0 0 0 0 1 x x x
0 0 0 1 0 0 0 0 x x x
0 0 0 1 0 0 0 1 0 0 x
0 0 0 0 0 0 0 0 0 x x
0 0 0 0 0 0 0 1 0 x x
0 0 0 0 0 0 0 0 0 x x
0 0 0 0 0 0 0 1 0 x x
0 0 0 0 0 0 0 0 0 x x
0 0 0 0 0 0 0 1 0 x x
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*/

/* Test case 08_P08T01:
M N progIn reset progLoad start result clk valid done output
0 0 0 0 0 0 0 0 x x x
0 0 0 0 0 0 0 1 x x x
0 0 0 1 0 0 0 0 x x x
0 0 0 1 0 0 0 1 0 0 x
0 0 0 0 0 0 0 0 0 x x
0 0 0 0 0 0 0 1 0 x x
0 0 0 0 0 0 0 0 0 x x
0 0 0 0 0 0 0 1 0 x x
0 0 0 0 0 0 0 0 0 x x
0 0 0 0 0 0 0 1 0 x x
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*/

/* Test case 02_P02T01:
M N progIn reset progLoad start result clk valid done output
0 0 0 0 0 0 0 0 x x x
0 0 0 0 0 0 0 1 x x x
0 0 0 1 0 0 0 0 x x x
0 0 0 1 0 0 0 1 0 0 x
0 0 0 0 0 0 0 0 0 x x
0 0 0 0 0 0 0 1 0 x x
0 0 0 0 0 0 0 0 0 x x
0 0 0 0 0 0 0 1 0 x x
0 0 0 0 0 0 0 0 0 x x
0 0 0 0 0 0 0 1 0 x x
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*/

/* Test case 13_P13T01:
M N progIn reset progLoad start result clk valid done output
0 0 0 0 0 0 0 0 x x x
0 0 0 0 0 0 0 1 x x x
0 0 0 1 0 0 0 0 x x x
0 0 0 1 0 0 0 1 0 0 x
0 0 0 0 0 0 0 0 0 x x
0 0 0 0 0 0 0 1 0 x x
0 0 0 0 0 0 0 0 0 x x
0 0 0 0 0 0 0 1 0 x x
0 0 0 0 0 0 0 0 0 x x
0 0 0 0 0 0 0 1 0 x x
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*/

/* Test case 07_P07T01:
M N progIn reset progLoad start result clk valid done output
0 0 0 0 0 0 0 0 x x x
0 0 0 0 0 0 0 1 x x x
0 0 0 1 0 0 0 0 x x x
0 0 0 1 0 0 0 1 0 0 x
0 0 0 0 0 0 0 0 0 x x
0 0 0 0 0 0 0 1 0 x x
0 0 0 0 0 0 0 0 0 x x
0 0 0 0 0 0 0 1 0 x x
0 0 0 0 0 0 0 0 0 x x
0 0 0 0 0 0 0 1 0 x x
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*/

/* Test case 01_P01T01:
M N progIn reset progLoad start result clk valid done output
0 0 0 0 0 0 0 0 x x x
0 0 0 0 0 0 0 1 x x x
0 0 0 1 0 0 0 0 x x x
0 0 0 1 0 0 0 1 0 0 x
0 0 0 0 0 0 0 0 0 x x
0 0 0 0 0 0 0 1 0 x x
0 0 0 0 0 0 0 0 0 x x
0 0 0 0 0 0 0 1 0 x x
0 0 0 0 0 0 0 0 0 x x
0 0 0 0 0 0 0 1 0 x x
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*/
