// Digital circuit final project.dig as structural Verilog
module final_project (
  input  [7:0] M,
  input  [7:0] N,
  input  [13:0] progIn,
  input  reset,
  input  progLoad,
  input  start,
  input  result,
  input  clk,
  output valid,
  output done,
  output [7:0] \output 
);

  wire accA_en, accB_en, and_1_out, and_2_out, and_3_out, and_4_out, and_5_out, and_10_out, and_11_out,
       and_13_out, and_16_out, and_17_out, and_19_out, and_20_out, branch_taken, clr_res_cnt, comp_eq,
       comp_gr, comp_ls, comparator_1_eq, comparator_3_eq, comparator_4_eq, comparator_5_eq, comparator_6_eq,
       comparator_7_eq, comparator_8_eq, comparator_9_eq, comparator_10_eq, comparator_11_eq,
       comparator_12_eq, comparator_13_eq, comparator_14_eq, cpu_running, fetch_cycle, fib_step, flag_eq,
       flag_eq_en, flag_gr, flag_gr_en, flag_ls, flag_ls_en, fsm_state, ir_en, is_add, is_and, is_cmp,
       is_djnz, is_exec, is_fib, is_fib_step0, is_gcd, is_is_prime, is_jeq, is_jgr, is_jls, is_jmp,
       is_load_A_imm, is_load_B_imm, is_load_C_M, is_load_D_N, is_mov_A_B, is_mov_A_C, is_mov_A_D,
       is_mov_A_SP, is_mov_B_A, is_mov_C_A, is_mov_D_A, is_mul, is_not, is_or, is_pop, is_prime_out, is_push,
       is_read_pRAM, is_read_rRAM, is_read_rRAM_C, is_read_rRAM_imm, is_regC_addr, is_res_active, is_stop,
       is_sub, is_write_rRAM_C, is_write_rRAM_imm, is_xor, multiplexer_32_out, next_flag_eq, next_flag_gr,
       next_flag_ls, nor_2_out, not_1_out, not_2_out, not_5_out, not_6_out, not_7_out, not_8_out, not_9_out,
       not_10_out, not_11_out, not_progLoad, not_rst, not_rst_start, or_3_out, or_4_out, or_5_out, or_6_out,
       or_7_out, or_8_out, or_9_out, or_10_out, or_12_out, or_13_out, or_14_out, or_17_out, or_19_out,
       or_20_out, or_21_out, or_22_out, or_23_out, or_25_out, or_26_out, or_27_out, or_28_out, or_29_out,
       or_31_out, or_32_out, or_33_out, or_35_out, or_36_out, or_37_out, or_38_out, or_39_out, or_40_out,
       or_41_out, or_42_out, or_44_out, or_47_out, or_49_out, or_53_out, PC_en, regC_en, regD_en,
       res_cnt_ovf, res_streaming, rRAM_ld, rRAM_str, rst_clearing, rst_cnt_ovf, rst_or_start, SP_en,
       take_djnz, take_jeq, take_jgr, take_jls;
  wire [3:0] res_addr_4b, rst_addr_4b;
  wire [5:0] multiplexer_41_out, opcode;
  wire [7:0] accA, accB, alu_and, alu_diff, alu_not, alu_or, alu_prod, alu_sum, alu_xor, div_1_r, div_2_r,
       div_3_r, div_4_r, div_5_r, div_6_r, div_7_r, div_8_r, div_9_r, div_10_r, div_11_r, div_12_r, fib_addr,
       fib_data, fib_high8, fib_low8, gcd_a_1, gcd_a_2, gcd_a_3, gcd_a_4, gcd_a_5, gcd_a_6, gcd_a_7, gcd_a_8,
       gcd_a_9, gcd_a_10, gcd_a_11, gcd_a_12, gcd_b_1, gcd_b_2, gcd_b_3, gcd_b_4, gcd_b_5, gcd_b_6, gcd_b_7,
       gcd_b_8, gcd_b_9, gcd_b_10, gcd_b_11, gcd_b_12, load_addr, multiplexer_1_out, multiplexer_2_out,
       multiplexer_3_out, multiplexer_5_out, multiplexer_7_out, multiplexer_8_out, multiplexer_9_out,
       multiplexer_11_out, multiplexer_12_out, multiplexer_13_out, multiplexer_14_out, multiplexer_15_out,
       multiplexer_16_out, multiplexer_17_out, multiplexer_18_out, multiplexer_19_out, multiplexer_20_out,
       multiplexer_21_out, multiplexer_23_out, multiplexer_24_out, multiplexer_25_out, multiplexer_26_out,
       multiplexer_28_out, multiplexer_29_out, multiplexer_30_out, multiplexer_31_out, multiplexer_36_out,
       next_accA, next_accB, next_PC, next_regC, next_regD, next_SP, operand, PC, PC_plus1, pRAM_addr, regC,
       regD, regD_minus1, rRAM_addr, rRAM_Din, SP, SP_minus1, SP_plus1;
  wire [13:0] pRAM_D;
  wire [15:0] fib_2, fib_3, fib_4, fib_5, fib_6, fib_7, fib_8, fib_9, fib_10, fib_11, fib_12, fib_13, fib_14,
       fib_15, fib_16, fib_17, fib_18, fib_19, fib_20, fib_21, fib_22, fib_23, fib_24;

  not not_1 (not_1_out, rst_cnt_ovf);
  not not_2 (not_2_out, res_cnt_ovf);
  and and_1 (and_1_out, res_streaming, res_cnt_ovf);
  nor nor_1 (not_rst_start, reset, start);
  not not_3 (not_rst, reset);
  or or_1 (is_res_active, result, res_streaming);
  or or_2 (is_regC_addr, is_write_rRAM_C, is_read_rRAM_C);
  or or_3 (or_3_out, rst_clearing, is_write_rRAM_imm);
  or or_4 (or_4_out, is_res_active, is_read_rRAM_imm);
  and and_2 (and_2_out, rst_clearing, not_1_out);
  and and_3 (and_3_out, res_streaming, not_2_out);
  RAMDualPort #(.AddrBits(8), .Bits(14)) pRAM (
    .A(pRAM_addr), .Din(progIn), .str(progLoad), .C(clk), .ld(not_progLoad), .D(pRAM_D));
  not not_4 (not_progLoad, progLoad);
  Counter #(.Bits(8)) Load_Cnt (.en(progLoad), .C(clk), .clr(reset), .out(load_addr));  // open: ovf
  or or_5 (or_5_out, reset, and_2_out);
  or or_6 (or_6_out, result, and_3_out);
  or or_7 (or_7_out, done, and_1_out);
  or or_8 (or_8_out, or_3_out, is_write_rRAM_C);
  or or_9 (or_9_out, or_4_out, is_read_rRAM_C);
  and and_4 (and_4_out, or_7_out, not_rst_start);
  RAMDualPort #(.AddrBits(8), .Bits(8)) rRAM (
    .A(rRAM_addr), .Din(rRAM_Din), .str(rRAM_str), .C(clk), .ld(rRAM_ld), .D(\output ));
  Multiplexer #(.Bits(8)) multiplexer_1 (.sel(is_read_pRAM), .in_0(PC), .in_1(operand), .out(multiplexer_1_out));
  D_FF Rst_FSM (.D(or_5_out), .C(clk), .Q(rst_clearing));  // open: nQ
  and and_5 (and_5_out, not_rst, or_6_out);
  Multiplexer #(.Bits(8)) multiplexer_2 (.sel(is_regC_addr), .in_0(operand), .in_1(regC), .out(multiplexer_2_out));
  Multiplexer #(.Bits(8)) multiplexer_3 (.sel(is_fib), .in_0(accA), .in_1(fib_data), .out(multiplexer_3_out));
  or or_10 (or_10_out, or_8_out, is_push);
  or or_11 (rRAM_ld, or_9_out, is_pop);
  or or_12 (or_12_out, is_read_rRAM_imm, is_read_rRAM_C);
  or or_13 (or_13_out, reset, is_load_A_imm);
  Multiplexer #(.Bits(8)) multiplexer_4 (.sel(progLoad), .in_0(multiplexer_1_out), .in_1(load_addr), .out(pRAM_addr));
  D_FF Res_FSM (.D(and_5_out), .C(clk), .Q(res_streaming));  // open: nQ
  nor nor_2 (nor_2_out, res_streaming, result);
  or or_14 (or_14_out, reset, start);
  D_FF Done_FF (.D(and_4_out), .C(clk), .Q(done));  // open: nQ
  Multiplexer #(.Bits(8)) multiplexer_5 (.sel(is_pop), .in_0(multiplexer_2_out), .in_1(SP), .out(multiplexer_5_out));
  Multiplexer #(.Bits(8)) multiplexer_6 (
    .sel(rst_clearing), .in_0(multiplexer_3_out), .in_1({8{1'b0}}), .out(rRAM_Din));
  Counter #(.Bits(4)) Rst_Cnt (.en(rst_clearing), .C(clk), .clr(reset), .out(rst_addr_4b), .ovf(rst_cnt_ovf));
  Multiplexer #(.Bits(8)) multiplexer_7 (
    .sel(is_push), .in_0(multiplexer_5_out), .in_1(SP_minus1), .out(multiplexer_7_out));
  or or_15 (rRAM_str, or_10_out, is_fib);
  or or_16 (is_read_rRAM, or_12_out, is_pop);
  or or_17 (or_17_out, or_13_out, is_mov_A_B);
  Counter #(.Bits(4)) Res_Cnt (.en(res_streaming), .C(clk), .clr(clr_res_cnt), .out(res_addr_4b), .ovf(res_cnt_ovf));
  or or_18 (clr_res_cnt, nor_2_out, or_14_out);
  Multiplexer #(.Bits(8)) multiplexer_8 (
    .sel(is_fib), .in_0(multiplexer_7_out), .in_1(fib_addr), .out(multiplexer_8_out));
  Seven_Seg_Hex seven_seg_hex_1 (.d(\output [7:4]), .dp(1'b0));
  Multiplexer #(.Bits(8)) multiplexer_9 (
    .sel(is_res_active), .in_0(multiplexer_8_out), .in_1({4'b0000, res_addr_4b}), .out(multiplexer_9_out));
  or or_19 (or_19_out, or_17_out, is_mov_A_C);
  Multiplexer #(.Bits(8)) multiplexer_10 (
    .sel(rst_clearing), .in_0(multiplexer_9_out), .in_1({4'b0000, rst_addr_4b}), .out(rRAM_addr));
  Multiplexer #(.Bits(8)) multiplexer_11 (.sel(is_mov_A_B), .in_0(operand), .in_1(accB), .out(multiplexer_11_out));
  or or_20 (or_20_out, or_19_out, is_mov_A_D);
  Seven_Seg_Hex seven_seg_hex_2 (.d(\output [3:0]), .dp(1'b0));
  Multiplexer #(.Bits(8)) multiplexer_12 (
    .sel(is_mov_A_C), .in_0(multiplexer_11_out), .in_1(regC), .out(multiplexer_12_out));
  Multiplexer #(.Bits(8)) multiplexer_13 (
    .sel(is_mov_A_D), .in_0(multiplexer_12_out), .in_1(regD), .out(multiplexer_13_out));
  or or_21 (or_21_out, or_20_out, is_mov_A_SP);
  Multiplexer #(.Bits(8)) multiplexer_14 (
    .sel(is_mov_A_SP), .in_0(multiplexer_13_out), .in_1(SP), .out(multiplexer_14_out));
  not not_5 (not_5_out, is_stop);
  not not_6 (not_6_out, fib_step);
  not not_7 (not_7_out, fsm_state);
  and and_6 (is_exec, cpu_running, fsm_state);
  not not_8 (not_8_out, fib_step);
  or or_22 (or_22_out, valid, is_stop);
  not not_9 (not_9_out, fsm_state);
  Add #(.Bits(8)) add_1 (.a(PC), .b(8'h1), .c_i(1'b0), .s(PC_plus1));  // open: c_o
  and and_7 (take_jeq, is_jeq, flag_eq);
  and and_8 (take_jgr, is_jgr, flag_gr);
  and and_9 (take_jls, is_jls, flag_ls);
  Comparator #(.Bits(8)) comparator_1 (.a(regD_minus1), .b({8{1'b0}}), .eq(comparator_1_eq));  // open: gt, lt
  or or_23 (or_23_out, is_jmp, take_jeq);
  or or_24 (rst_or_start, reset, start);
  not not_10 (not_10_out, fsm_state);
  or or_25 (or_25_out, rst_or_start, fetch_cycle);
  Multiplexer #(.Bits(8)) multiplexer_15 (
    .sel(is_read_rRAM), .in_0(multiplexer_14_out), .in_1(\output ), .out(multiplexer_15_out));
  or or_26 (or_26_out, or_21_out, is_read_rRAM);
  and and_10 (and_10_out, cpu_running, not_5_out);
  and and_11 (and_11_out, is_fib, not_6_out);
  or or_27 (or_27_out, not_7_out, is_fib_step0);
  and and_12 (is_fib_step0, is_fib, not_8_out);
  and and_13 (and_13_out, not_rst_start, or_22_out);
  and and_14 (ir_en, cpu_running, not_9_out);
  not not_11 (not_11_out, comparator_1_eq);
  and and_15 (fetch_cycle, cpu_running, not_10_out);
  Multiplexer #(.Bits(8)) multiplexer_16 (
    .sel(is_read_pRAM), .in_0(multiplexer_15_out), .in_1(pRAM_D[7:0]), .out(multiplexer_16_out));
  or or_28 (or_28_out, start, and_10_out);
  and and_16 (and_16_out, and_11_out, not_rst_start);
  and and_17 (and_17_out, cpu_running, or_27_out);
  and and_18 (take_djnz, not_11_out, is_djnz);
  or or_29 (or_29_out, or_23_out, take_jgr);
  or or_30 (PC_en, or_25_out, branch_taken);
  Multiplexer #(.Bits(8)) multiplexer_17 (
    .sel(is_add), .in_0(multiplexer_16_out), .in_1(alu_sum), .out(multiplexer_17_out));
  or or_31 (or_31_out, or_26_out, is_read_pRAM);
  and and_19 (and_19_out, not_rst, or_28_out);
  D_FF Fib_Seq (.D(and_13_out), .C(clk), .Q(valid));  // open: nQ
  Register #(.Bits(14)) IR_14b (.D(pRAM_D), .C(clk), .en(ir_en), .Q({opcode, operand}));
  or or_32 (or_32_out, or_29_out, take_jls);
  Multiplexer #(.Bits(8)) multiplexer_18 (
    .sel(is_sub), .in_0(multiplexer_17_out), .in_1(alu_diff), .out(multiplexer_18_out));
  or or_33 (or_33_out, or_31_out, is_add);
  D_FF Fetch_Exec (.D(and_16_out), .C(clk), .Q(fib_step));  // open: nQ
  and and_20 (and_20_out, and_17_out, not_rst_start);
  Multiplexer #(.Bits(8)) multiplexer_19 (
    .sel(is_mul), .in_0(multiplexer_18_out), .in_1(alu_prod), .out(multiplexer_19_out));
  D_FF Run_FSM (.D(and_19_out), .C(clk), .Q(cpu_running));  // open: nQ
  D_FF Valid_FF (.D(and_20_out), .C(clk), .Q(fsm_state));  // open: nQ
  Multiplexer #(.Bits(8)) multiplexer_20 (
    .sel(branch_taken), .in_0(PC_plus1), .in_1(operand), .out(multiplexer_20_out));
  or or_34 (branch_taken, or_32_out, take_djnz);
  Multiplexer #(.Bits(8)) multiplexer_21 (
    .sel(is_and), .in_0(multiplexer_19_out), .in_1(alu_and), .out(multiplexer_21_out));
  or or_35 (or_35_out, or_33_out, is_sub);
  Multiplexer #(.Bits(8)) multiplexer_22 (
    .sel(rst_or_start), .in_0(multiplexer_20_out), .in_1({8{1'b0}}), .out(next_PC));
  Register #(.Bits(8)) u_accA (.D(next_accA), .C(clk), .en(accA_en), .Q(accA));
  Multiplexer #(.Bits(8)) multiplexer_23 (
    .sel(is_or), .in_0(multiplexer_21_out), .in_1(alu_or), .out(multiplexer_23_out));
  Multiplexer #(.Bits(8)) multiplexer_24 (
    .sel(is_xor), .in_0(multiplexer_23_out), .in_1(alu_xor), .out(multiplexer_24_out));
  or or_36 (or_36_out, or_35_out, is_mul);
  Register #(.Bits(8)) u_PC (.D(next_PC), .C(clk), .en(PC_en), .Q(PC));
  Multiplexer #(.Bits(8)) multiplexer_25 (
    .sel(is_not), .in_0(multiplexer_24_out), .in_1(alu_not), .out(multiplexer_25_out));
  Multiplexer #(.Bits(8)) multiplexer_26 (
    .sel(is_gcd), .in_0(multiplexer_25_out), .in_1(gcd_a_12), .out(multiplexer_26_out));
  or or_37 (or_37_out, or_36_out, is_and);
  Multiplexer #(.Bits(8)) multiplexer_27 (.sel(reset), .in_0(multiplexer_26_out), .in_1({8{1'b0}}), .out(next_accA));
  or or_38 (or_38_out, or_37_out, is_or);
  Sub #(.Bits(8)) sub_1 (.a(SP), .b(8'h1), .c_i(1'b0), .s(SP_minus1));  // open: c_o
  Add #(.Bits(8)) add_2 (.a(SP), .b(8'h1), .c_i(1'b0), .s(SP_plus1));  // open: c_o
  or or_39 (or_39_out, rst_or_start, is_push);
  Sub #(.Bits(8)) sub_2 (.a(regD), .b(8'h1), .c_i(1'b0), .s(regD_minus1));  // open: c_o
  or or_40 (or_40_out, reset, is_mov_D_A);
  or or_41 (or_41_out, reset, is_mov_C_A);
  or or_42 (or_42_out, reset, is_load_B_imm);
  Add #(.Bits(8)) add_3 (.a(accA), .b(accB), .c_i(1'b0), .s(alu_sum));  // open: c_o
  Sub #(.Bits(8)) sub_3 (.a(accA), .b(accB), .c_i(1'b0), .s(alu_diff));  // open: c_o
  assign alu_and = accA & accB;  // And and_21, 8 bits wide
  assign alu_or = accA | accB;  // Or or_43, 8 bits wide
  assign alu_xor = accA ^ accB;  // XOr xor_1, 8 bits wide
  assign alu_not = ~accA;  // Not not_12, 8 bits wide
  Comparator #(.Bits(8), .\signed ("true")) comparator_2 (.a(accA), .b(accB), .gt(comp_gr), .eq(comp_eq), .lt(comp_ls));
  ROM #(.AddrBits(8), .Bits(1)) rom_1 (.A(accA), .sel(1'b1), .D(is_prime_out));
  or or_44 (or_44_out, reset, is_cmp);
  or or_45 (flag_gr_en, reset, is_cmp);
  or or_46 (flag_ls_en, reset, is_cmp);
  or or_47 (or_47_out, or_38_out, is_xor);
  or or_48 (SP_en, or_39_out, is_pop);
  or or_49 (or_49_out, or_40_out, is_load_D_N);
  or or_50 (regC_en, or_41_out, is_load_C_M);
  or or_51 (accB_en, or_42_out, is_mov_B_A);
  Mul #(.Bits(4)) mul_1 (.a(accA[3:0]), .b(accB[3:0]), .mul(alu_prod));
  or or_52 (flag_eq_en, or_44_out, is_is_prime);
  or or_53 (or_53_out, or_47_out, is_not);
  or or_54 (regD_en, or_49_out, is_djnz);
  or or_55 (accA_en, or_53_out, is_gcd);
  Multiplexer #(.Bits(8)) multiplexer_28 (.sel(is_push), .in_0(SP_plus1), .in_1(SP_minus1), .out(multiplexer_28_out));
  Multiplexer #(.Bits(8)) multiplexer_29 (.sel(is_load_D_N), .in_0(accA), .in_1(N), .out(multiplexer_29_out));
  Multiplexer #(.Bits(8)) multiplexer_30 (.sel(is_load_C_M), .in_0(accA), .in_1(M), .out(multiplexer_30_out));
  Multiplexer #(.Bits(8)) multiplexer_31 (.sel(is_mov_B_A), .in_0(operand), .in_1(accA), .out(multiplexer_31_out));
  Multiplexer #(.Bits(1)) multiplexer_32 (
    .sel(is_is_prime), .in_0(comp_eq), .in_1(is_prime_out), .out(multiplexer_32_out));
  Multiplexer #(.Bits(1)) multiplexer_33 (.sel(reset), .in_0(comp_gr), .in_1(1'b0), .out(next_flag_gr));
  Multiplexer #(.Bits(1)) multiplexer_34 (.sel(reset), .in_0(comp_ls), .in_1(1'b0), .out(next_flag_ls));
  Multiplexer #(.Bits(8)) multiplexer_35 (
    .sel(rst_or_start), .in_0(multiplexer_28_out), .in_1({8{1'b0}}), .out(next_SP));
  Multiplexer #(.Bits(8)) multiplexer_36 (
    .sel(is_djnz), .in_0(multiplexer_29_out), .in_1(regD_minus1), .out(multiplexer_36_out));
  Multiplexer #(.Bits(8)) multiplexer_37 (.sel(reset), .in_0(multiplexer_30_out), .in_1({8{1'b0}}), .out(next_regC));
  Multiplexer #(.Bits(8)) multiplexer_38 (.sel(reset), .in_0(multiplexer_31_out), .in_1({8{1'b0}}), .out(next_accB));
  Multiplexer #(.Bits(1)) multiplexer_39 (.sel(reset), .in_0(multiplexer_32_out), .in_1(1'b0), .out(next_flag_eq));
  Multiplexer #(.Bits(8)) multiplexer_40 (.sel(reset), .in_0(multiplexer_36_out), .in_1({8{1'b0}}), .out(next_regD));
  Register #(.Bits(8)) u_SP (.D(next_SP), .C(clk), .en(SP_en), .Q(SP));
  Register #(.Bits(8)) u_regD (.D(next_regD), .C(clk), .en(regD_en), .Q(regD));
  Register #(.Bits(8)) u_regC (.D(next_regC), .C(clk), .en(regC_en), .Q(regC));
  Register #(.Bits(8)) u_accB (.D(next_accB), .C(clk), .en(accB_en), .Q(accB));
  Register #(.Bits(1)) u_flag_eq (.D(next_flag_eq), .C(clk), .en(flag_eq_en), .Q(flag_eq));
  Register #(.Bits(1)) u_flag_gr (.D(next_flag_gr), .C(clk), .en(flag_gr_en), .Q(flag_gr));
  Register #(.Bits(1)) u_flag_ls (.D(next_flag_ls), .C(clk), .en(flag_ls_en), .Q(flag_ls));
  Multiplexer #(.Bits(6)) multiplexer_41 (.sel(is_exec), .in_0({6{1'b0}}), .in_1(opcode), .out(multiplexer_41_out));
  Decoder #(.Selector_Bits(6)) decoder_1 (
    .sel(multiplexer_41_out), .out_1(is_load_A_imm), .out_2(is_load_B_imm), .out_4(is_mov_A_B),
    .out_5(is_mov_B_A), .out_6(is_mov_C_A), .out_7(is_mov_D_A), .out_8(is_mov_A_C), .out_9(is_mov_A_D),
    .out_10(is_mov_A_SP), .out_12(is_load_C_M), .out_13(is_load_D_N), .out_16(is_read_rRAM_imm),
    .out_17(is_write_rRAM_imm), .out_18(is_read_pRAM), .out_20(is_read_rRAM_C), .out_21(is_write_rRAM_C),
    .out_24(is_push), .out_25(is_pop), .out_32(is_add), .out_33(is_sub), .out_34(is_mul), .out_40(is_and),
    .out_41(is_or), .out_42(is_xor), .out_43(is_not), .out_48(is_jmp), .out_49(is_jeq), .out_50(is_jgr),
    .out_51(is_jls), .out_52(is_djnz), .out_56(is_cmp), .out_57(is_is_prime), .out_60(is_gcd),
    .out_61(is_fib), .out_63(is_stop));  // open: out_0, out_3, out_11, out_14, out_15, out_19, out_22, out_23, out_26, out_27, out_28, out_29, out_30, out_31, out_35, out_36, out_37, out_38, out_39, out_44, out_45, out_46, out_47, out_53, out_54, out_55, out_58, out_59, out_62
  Div #(.Bits(8)) div_1 (.a(accA), .b(accB), .r(div_1_r));  // open: q
  Comparator #(.Bits(8)) comparator_3 (.a(accB), .b({8{1'b0}}), .eq(comparator_3_eq));  // open: gt, lt
  Div #(.Bits(8)) div_2 (.a(gcd_a_1), .b(gcd_b_1), .r(div_2_r));  // open: q
  Comparator #(.Bits(8)) comparator_4 (.a(gcd_b_1), .b({8{1'b0}}), .eq(comparator_4_eq));  // open: gt, lt
  Div #(.Bits(8)) div_3 (.a(gcd_a_2), .b(gcd_b_2), .r(div_3_r));  // open: q
  Comparator #(.Bits(8)) comparator_5 (.a(gcd_b_2), .b({8{1'b0}}), .eq(comparator_5_eq));  // open: gt, lt
  Div #(.Bits(8)) div_4 (.a(gcd_a_3), .b(gcd_b_3), .r(div_4_r));  // open: q
  Comparator #(.Bits(8)) comparator_6 (.a(gcd_b_3), .b({8{1'b0}}), .eq(comparator_6_eq));  // open: gt, lt
  Div #(.Bits(8)) div_5 (.a(gcd_a_4), .b(gcd_b_4), .r(div_5_r));  // open: q
  Comparator #(.Bits(8)) comparator_7 (.a(gcd_b_4), .b({8{1'b0}}), .eq(comparator_7_eq));  // open: gt, lt
  Div #(.Bits(8)) div_6 (.a(gcd_a_5), .b(gcd_b_5), .r(div_6_r));  // open: q
  Comparator #(.Bits(8)) comparator_8 (.a(gcd_b_5), .b({8{1'b0}}), .eq(comparator_8_eq));  // open: gt, lt
  Div #(.Bits(8)) div_7 (.a(gcd_a_6), .b(gcd_b_6), .r(div_7_r));  // open: q
  Comparator #(.Bits(8)) comparator_9 (.a(gcd_b_6), .b({8{1'b0}}), .eq(comparator_9_eq));  // open: gt, lt
  Div #(.Bits(8)) div_8 (.a(gcd_a_7), .b(gcd_b_7), .r(div_8_r));  // open: q
  Comparator #(.Bits(8)) comparator_10 (.a(gcd_b_7), .b({8{1'b0}}), .eq(comparator_10_eq));  // open: gt, lt
  Div #(.Bits(8)) div_9 (.a(gcd_a_8), .b(gcd_b_8), .r(div_9_r));  // open: q
  Comparator #(.Bits(8)) comparator_11 (.a(gcd_b_8), .b({8{1'b0}}), .eq(comparator_11_eq));  // open: gt, lt
  Div #(.Bits(8)) div_10 (.a(gcd_a_9), .b(gcd_b_9), .r(div_10_r));  // open: q
  Comparator #(.Bits(8)) comparator_12 (.a(gcd_b_9), .b({8{1'b0}}), .eq(comparator_12_eq));  // open: gt, lt
  Div #(.Bits(8)) div_11 (.a(gcd_a_10), .b(gcd_b_10), .r(div_11_r));  // open: q
  Comparator #(.Bits(8)) comparator_13 (.a(gcd_b_10), .b({8{1'b0}}), .eq(comparator_13_eq));  // open: gt, lt
  Div #(.Bits(8)) div_12 (.a(gcd_a_11), .b(gcd_b_11), .r(div_12_r));  // open: q
  Comparator #(.Bits(8)) comparator_14 (.a(gcd_b_11), .b({8{1'b0}}), .eq(comparator_14_eq));  // open: gt, lt
  Multiplexer #(.Bits(8)) multiplexer_42 (.sel(comparator_3_eq), .in_0(accB), .in_1(accA), .out(gcd_a_1));
  Multiplexer #(.Bits(8)) multiplexer_43 (.sel(comparator_3_eq), .in_0(div_1_r), .in_1({8{1'b0}}), .out(gcd_b_1));
  Multiplexer #(.Bits(8)) multiplexer_44 (.sel(comparator_4_eq), .in_0(gcd_b_1), .in_1(gcd_a_1), .out(gcd_a_2));
  Multiplexer #(.Bits(8)) multiplexer_45 (.sel(comparator_4_eq), .in_0(div_2_r), .in_1({8{1'b0}}), .out(gcd_b_2));
  Multiplexer #(.Bits(8)) multiplexer_46 (.sel(comparator_5_eq), .in_0(gcd_b_2), .in_1(gcd_a_2), .out(gcd_a_3));
  Multiplexer #(.Bits(8)) multiplexer_47 (.sel(comparator_5_eq), .in_0(div_3_r), .in_1({8{1'b0}}), .out(gcd_b_3));
  Multiplexer #(.Bits(8)) multiplexer_48 (.sel(comparator_6_eq), .in_0(gcd_b_3), .in_1(gcd_a_3), .out(gcd_a_4));
  Multiplexer #(.Bits(8)) multiplexer_49 (.sel(comparator_6_eq), .in_0(div_4_r), .in_1({8{1'b0}}), .out(gcd_b_4));
  Multiplexer #(.Bits(8)) multiplexer_50 (.sel(comparator_7_eq), .in_0(gcd_b_4), .in_1(gcd_a_4), .out(gcd_a_5));
  Multiplexer #(.Bits(8)) multiplexer_51 (.sel(comparator_7_eq), .in_0(div_5_r), .in_1({8{1'b0}}), .out(gcd_b_5));
  Multiplexer #(.Bits(8)) multiplexer_52 (.sel(comparator_8_eq), .in_0(gcd_b_5), .in_1(gcd_a_5), .out(gcd_a_6));
  Multiplexer #(.Bits(8)) multiplexer_53 (.sel(comparator_8_eq), .in_0(div_6_r), .in_1({8{1'b0}}), .out(gcd_b_6));
  Multiplexer #(.Bits(8)) multiplexer_54 (.sel(comparator_9_eq), .in_0(gcd_b_6), .in_1(gcd_a_6), .out(gcd_a_7));
  Multiplexer #(.Bits(8)) multiplexer_55 (.sel(comparator_9_eq), .in_0(div_7_r), .in_1({8{1'b0}}), .out(gcd_b_7));
  Multiplexer #(.Bits(8)) multiplexer_56 (.sel(comparator_10_eq), .in_0(gcd_b_7), .in_1(gcd_a_7), .out(gcd_a_8));
  Multiplexer #(.Bits(8)) multiplexer_57 (.sel(comparator_10_eq), .in_0(div_8_r), .in_1({8{1'b0}}), .out(gcd_b_8));
  Multiplexer #(.Bits(8)) multiplexer_58 (.sel(comparator_11_eq), .in_0(gcd_b_8), .in_1(gcd_a_8), .out(gcd_a_9));
  Multiplexer #(.Bits(8)) multiplexer_59 (.sel(comparator_11_eq), .in_0(div_9_r), .in_1({8{1'b0}}), .out(gcd_b_9));
  Multiplexer #(.Bits(8)) multiplexer_60 (.sel(comparator_12_eq), .in_0(gcd_b_9), .in_1(gcd_a_9), .out(gcd_a_10));
  Multiplexer #(.Bits(8)) multiplexer_61 (.sel(comparator_12_eq), .in_0(div_10_r), .in_1({8{1'b0}}), .out(gcd_b_10));
  Multiplexer #(.Bits(8)) multiplexer_62 (.sel(comparator_13_eq), .in_0(gcd_b_10), .in_1(gcd_a_10), .out(gcd_a_11));
  Multiplexer #(.Bits(8)) multiplexer_63 (.sel(comparator_13_eq), .in_0(div_11_r), .in_1({8{1'b0}}), .out(gcd_b_11));
  Multiplexer #(.Bits(8)) multiplexer_64 (.sel(comparator_14_eq), .in_0(gcd_b_11), .in_1(gcd_a_11), .out(gcd_a_12));
  Multiplexer #(.Bits(8)) multiplexer_65 (.sel(comparator_14_eq), .in_0(div_12_r), .in_1({8{1'b0}}), .out(gcd_b_12));
  Add #(.Bits(16)) add_4 (.a({16{1'b0}}), .b(16'h1), .c_i(1'b0), .s(fib_2));  // open: c_o
  Add #(.Bits(16)) add_5 (.a(16'h1), .b(fib_2), .c_i(1'b0), .s(fib_3));  // open: c_o
  Add #(.Bits(16)) add_6 (.a(fib_2), .b(fib_3), .c_i(1'b0), .s(fib_4));  // open: c_o
  Add #(.Bits(16)) add_7 (.a(fib_3), .b(fib_4), .c_i(1'b0), .s(fib_5));  // open: c_o
  Add #(.Bits(16)) add_8 (.a(fib_4), .b(fib_5), .c_i(1'b0), .s(fib_6));  // open: c_o
  Add #(.Bits(16)) add_9 (.a(fib_5), .b(fib_6), .c_i(1'b0), .s(fib_7));  // open: c_o
  Add #(.Bits(16)) add_10 (.a(fib_6), .b(fib_7), .c_i(1'b0), .s(fib_8));  // open: c_o
  Add #(.Bits(16)) add_11 (.a(fib_7), .b(fib_8), .c_i(1'b0), .s(fib_9));  // open: c_o
  Add #(.Bits(16)) add_12 (.a(fib_8), .b(fib_9), .c_i(1'b0), .s(fib_10));  // open: c_o
  Add #(.Bits(16)) add_13 (.a(fib_9), .b(fib_10), .c_i(1'b0), .s(fib_11));  // open: c_o
  Add #(.Bits(16)) add_14 (.a(fib_10), .b(fib_11), .c_i(1'b0), .s(fib_12));  // open: c_o
  Add #(.Bits(16)) add_15 (.a(fib_11), .b(fib_12), .c_i(1'b0), .s(fib_13));  // open: c_o
  Add #(.Bits(16)) add_16 (.a(fib_12), .b(fib_13), .c_i(1'b0), .s(fib_14));  // open: c_o
  Add #(.Bits(16)) add_17 (.a(fib_13), .b(fib_14), .c_i(1'b0), .s(fib_15));  // open: c_o
  Add #(.Bits(16)) add_18 (.a(fib_14), .b(fib_15), .c_i(1'b0), .s(fib_16));  // open: c_o
  Add #(.Bits(16)) add_19 (.a(fib_15), .b(fib_16), .c_i(1'b0), .s(fib_17));  // open: c_o
  Add #(.Bits(16)) add_20 (.a(fib_16), .b(fib_17), .c_i(1'b0), .s(fib_18));  // open: c_o
  Add #(.Bits(16)) add_21 (.a(fib_17), .b(fib_18), .c_i(1'b0), .s(fib_19));  // open: c_o
  Add #(.Bits(16)) add_22 (.a(fib_18), .b(fib_19), .c_i(1'b0), .s(fib_20));  // open: c_o
  Add #(.Bits(16)) add_23 (.a(fib_19), .b(fib_20), .c_i(1'b0), .s(fib_21));  // open: c_o
  Add #(.Bits(16)) add_24 (.a(fib_20), .b(fib_21), .c_i(1'b0), .s(fib_22));  // open: c_o
  Add #(.Bits(16)) add_25 (.a(fib_21), .b(fib_22), .c_i(1'b0), .s(fib_23));  // open: c_o
  Add #(.Bits(16)) add_26 (.a(fib_22), .b(fib_23), .c_i(1'b0), .s(fib_24));  // open: c_o
  Multiplexer #(.Bits(8)) multiplexer_66 (.sel(fib_step), .in_0(8'ha), .in_1(8'hb), .out(fib_addr));
  Multiplexer #(.Bits(8)) multiplexer_67 (.sel(fib_step), .in_0(fib_high8), .in_1(fib_low8), .out(fib_data));
  Multiplexer #(.Bits(16), .Selector_Bits(5)) multiplexer_68 (
    .sel(accA[4:0]), .in_0({16{1'b0}}), .in_1(16'h1), .in_2(fib_2), .in_3(fib_3), .in_4(fib_4), .in_5(fib_5),
    .in_6(fib_6), .in_7(fib_7), .in_8(fib_8), .in_9(fib_9), .in_10(fib_10), .in_11(fib_11), .in_12(fib_12),
    .in_13(fib_13), .in_14(fib_14), .in_15(fib_15), .in_16(fib_16), .in_17(fib_17), .in_18(fib_18),
    .in_19(fib_19), .in_20(fib_20), .in_21(fib_21), .in_22(fib_22), .in_23(fib_23), .in_24(fib_24),
    .in_25({16{1'b0}}), .in_26({16{1'b0}}), .in_27({16{1'b0}}), .in_28({16{1'b0}}), .in_29({16{1'b0}}),
    .in_30({16{1'b0}}), .in_31({16{1'b0}}), .out({fib_high8, fib_low8}));

  // Other names for the same wires on the sheet: fib_val_16b[15:0] = {fib_high8, fib_low8};
  //   accA_low4[3:0] = accA[3:0]; gcd_a_0[7:0] = accA; accB_low4[3:0] = accB[3:0]; gcd_b_0[7:0] = accB;
  //   gcd_res[7:0] = gcd_a_12; in_clk = clk; in_M[7:0] = M; in_N[7:0] = N; in_progIn[13:0] = progIn;
  //   in_progLoad = progLoad; in_result = result; in_rst = reset; in_start = start; out_done = done;
  //   out_valid = valid; pRAM_D_lower8[7:0] = pRAM_D[7:0]; res_addr_8b[3:0] = res_addr_4b; out_data[7:0] = \output ;
  //   rRAM_D[7:0] = \output ; rst_addr_8b[3:0] = rst_addr_4b

  // Notes on the sheet:
  //   2. หน่วยความจำข้อมูลและระบบส่งผลลัพธ์ (rRAM 256x8 & Result Streaming)
  //   *** CEDT Final Project 2569: 8-bit Multi-Cycle CPU Architecture (Complete 2D Presentation Layout) ***
  //   ออกแบบแยกเป็น 10 โซนฟังก์ชัน • โครงสร้าง Multi-Cycle (2-Cycle Fetch/Exec) • ปฏิบัติตามเกณฑ์ 100% (No ROM GCD/FIB, Single Port RAMDualPort)
  //   0. ส่วนเชื่อมต่ออินพุต/เอาต์พุตหลัก (Top-Level I/O & Bus Interface)
  //   1. หน่วยความจำคำสั่งและการโหลดโปรแกรม (pRAM 256x14 & Program Loader)
  //   6B. วงจรรวบรวมผลลัพธ์ของสะสม (Accumulator accA MUX & Datapath Matrix)
  //   3. วงจรควบคุมสถานะและรีจิสเตอร์คำสั่ง (CPU Core FSM & Instruction Register)
  //   5. ตัวนับคำสั่งและระบบกระโดด (Program Counter PC & Branch Logic)
  //   6A. กลุ่มรีจิสเตอร์หลัก (Primary Registers: SP, regD, regC, accB)
  //   7. หน่วยคำนวณและตรรกะ (ALU: Add, Sub, Mul 4-bit, And, Or, Xor, Not)
  //   8. ตัวเปรียบเทียบ แฟล็ก และตารางจำนวนเฉพาะ (Comparator, Flags & isPrime ROM)
  //   contents of rom_1 (hex, n*v repeats v):
  //   0,0,1,1,0,1,0,1,0,0,0,1,0,1,0,0,0,1,0,1,0,0,0,1,0,0,0,0,0,1,0,1,0,0,0,0,0,1,0,0,0,1,0,1,0,0,
  //   0,1,0,0,0,0,0,1,0,0,0,0,0,1,0,1,0,0,0,0,0,1,0,0,0,1,0,1,0,0,0,0,0,1,0,0,0,1,0,0,0,0,0,1,0,0,
  //   0,0,0,0,0,1,0,0,0,1,0,1,0,0,0,1,0,1,0,0,0,1,0,0,0,0,0,0,0,0,0,0,0,0,0,1,0,0,0,1,0,0,0,0,0,1,
  //   0,1,0,0,0,0,0,0,0,0,0,1,0,1,0,0,0,0,0,1,0,0,0,0,0,1,0,0,0,1,0,0,0,0,0,1,0,0,0,0,0,1,0,1,0,0,
  //   0,0,0,0,0,0,0,1,0,1,0,0,0,1,0,1,0,0,0,0,0,0,0,0,0,0,0,1,0,0,0,0,0,0,0,0,0,0,0,1,0,0,0,1,0,1,
  //   0,0,0,1,0,0,0,0,0,1,0,1,0,0,0,0,0,0,0,0,0,1,0,0,0,0
  //   4. วงจรถอดรหัสคำสั่ง (Opcode Decoder)
  //   9. วงจรคำนวณ ห.ร.ม. 12 สเตจ (GCD Accelerator)
  //   10. วงจรคำนวณฟีโบนัชชี 16 บิต (Fibonacci Accelerator)
endmodule

/* Test case 01_P01T01:
M N progIn reset progLoad start result clk valid done output
0 0 0 0 0 0 0 0 x x x
0 0 0 0 0 0 0 1 x x x
0 0 0 1 0 0 0 0 x x x
0 0 0 1 0 0 0 1 0 0 x
0 0 0 0 0 0 0 0 0 x x
0 0 0 0 0 0 0 1 0 x x
0 0 0 0 0 0 0 0 0 x x
0 0 0 0 0 0 0 1 0 x x
0 0 0 0 0 0 0 0 0 x x
0 0 0 0 0 0 0 1 0 x x
0 0 0 0 0 0 0 0 0 x x
0 0 0 0 0 0 0 1 0 x x
0 0 0 0 0 0 0 0 0 x x
0 0 0 0 0 0 0 1 0 x x
0 0 0 0 0 0 0 0 0 x x
0 0 0 0 0 0 0 1 0 x x
0 0 0 0 0 0 0 0 0 x x
0 0 0 0 0 0 0 1 0 x x
0 0 0 0 0 0 0 0 0 x x
0 0 0 0 0 0 0 1 0 x x
0 0 0 0 0 0 0 0 0 x x
0 0 0 0 0 0 0 1 0 x x
0 0 0 0 0 0 0 0 0 x x
0 0 0 0 0 0 0 1 0 x x
0 0 0 0 0 0 0 0 0 x x
0 0 0 0 0 0 0 1 0 x x
0 0 0 0 0 0 0 0 0 x x
0 0 0 0 0 0 0 1 0 x x
0 0 0 0 0 0 0 0 0 x x
0 0 0 0 0 0 0 1 0 x x
0 0 0 0 0 0 0 0 0 x x
0 0 0 0 0 0 0 1 0 x x
0 0 0 0 0 0 0 0 0 x x
0 0 0 0 0 0 0 1 0 x x
0 0 0 0 0 0 0 0 0 x x
0 0 0 0 0 0 0 1 0 x x
0 0 0 0 0 0 0 0 0 x x
0 0 0 0 0 0 0 1 0 x x
0 0 0 0 0 0 0 0 0 x x
0 0 0 0 0 0 0 1 0 x x
0 0 0 0 0 0 0 0 0 x x
0 0 0 0 0 0 0 1 0 x x
0 0 0 0 0 0 0 0 0 x x
0 0 0 0 0 0 0 1 0 x x
0 0 271 0 1 0 0 0 0 x x
0 0 271 0 1 0 0 1 0 x x
0 0 565 0 1 0 0 0 0 x x
0 0 565 0 1 0 0 1 0 x x
0 0 8192 0 1 0 0 0 0 x x
0 0 8192 0 1 0 0 1 0 x x
0 0 4355 0 1 0 0 0 0 x x
0 0 4355 0 1 0 0 1 0 x x
0 0 16128 0 1 0 0 0 0 x x
0 0 16128 0 1 0 0 1 0 x x
0 0 0 0 0 1 0 0 x x x
0 0 0 0 0 1 0 1 x 0 x
0 0 0 0 0 0 0 0 x 0 x
0 0 0 0 0 0 0 1 x 0 x
0 0 0 0 0 0 0 0 x 0 x
0 0 0 0 0 0 0 1 x 0 x
0 0 0 0 0 0 0 0 x 0 x
0 0 0 0 0 0 0 1 x 0 x
0 0 0 0 0 0 0 0 x 0 x
0 0 0 0 0 0 0 1 x 0 x
0 0 0 0 0 0 0 0 x 0 x
0 0 0 0 0 0 0 1 x 0 x
0 0 0 0 0 0 0 0 x 0 x
0 0 0 0 0 0 0 1 x 0 x
0 0 0 0 0 0 0 0 x 0 x
0 0 0 0 0 0 0 1 x 0 x
0 0 0 0 0 0 0 0 x 0 x
0 0 0 0 0 0 0 1 x 0 x
0 0 0 0 0 0 0 0 x 0 x
0 0 0 0 0 0 0 1 x 0 x
0 0 0 0 0 0 0 0 x 0 x
0 0 0 0 0 0 0 1 x 0 x
0 0 0 0 0 0 0 0 x 0 x
0 0 0 0 0 0 0 1 x 0 x
0 0 0 0 0 0 0 0 x 0 x
0 0 0 0 0 0 0 1 x 0 x
0 0 0 0 0 0 0 0 x 0 x
0 0 0 0 0 0 0 1 x 0 x
0 0 0 0 0 0 0 0 x 0 x
0 0 0 0 0 0 0 1 x 0 x
0 0 0 0 0 0 0 0 x 0 x
0 0 0 0 0 0 0 1 x 0 x
0 0 0 0 0 0 0 0 x 0 x
0 0 0 0 0 0 0 1 x 0 x
0 0 0 0 0 0 0 0 x 0 x
0 0 0 0 0 0 0 1 x 0 x
0 0 0 0 0 0 0 0 x 0 x
0 0 0 0 0 0 0 1 x 0 x
0 0 0 0 0 0 0 0 x 0 x
0 0 0 0 0 0 0 1 x 0 x
0 0 0 0 0 0 0 0 x 0 x
0 0 0 0 0 0 0 1 x 0 x
0 0 0 0 0 0 0 0 x 0 x
0 0 0 0 0 0 0 1 x 0 x
0 0 0 0 0 0 0 0 x 0 x
0 0 0 0 0 0 0 1 x 0 x
0 0 0 0 0 0 0 0 x 0 x
0 0 0 0 0 0 0 1 x 0 x
0 0 0 0 0 0 0 0 x 0 x
0 0 0 0 0 0 0 1 1 0 x
0 0 0 0 0 0 1 0 1 x x
0 0 0 0 0 0 1 1 1 0 0
0 0 0 0 0 0 0 0 1 0 0
0 0 0 0 0 0 0 1 1 0 0
0 0 0 0 0 0 0 0 1 0 0
0 0 0 0 0 0 0 1 1 0 0
0 0 0 0 0 0 0 0 1 0 0
0 0 0 0 0 0 0 1 1 0 68
0 0 0 0 0 0 0 0 1 0 68
0 0 0 0 0 0 0 1 1 0 0
0 0 0 0 0 0 0 0 1 0 0
0 0 0 0 0 0 0 1 1 0 0
0 0 0 0 0 0 0 0 1 0 0
0 0 0 0 0 0 0 1 1 0 0
0 0 0 0 0 0 0 0 1 0 0
0 0 0 0 0 0 0 1 1 0 0
0 0 0 0 0 0 0 0 1 0 0
0 0 0 0 0 0 0 1 1 0 0
0 0 0 0 0 0 0 0 1 0 0
0 0 0 0 0 0 0 1 1 0 0
0 0 0 0 0 0 0 0 1 0 0
0 0 0 0 0 0 0 1 1 0 0
0 0 0 0 0 0 0 0 1 0 0
0 0 0 0 0 0 0 1 1 0 0
0 0 0 0 0 0 0 0 1 0 0
0 0 0 0 0 0 0 1 1 0 0
0 0 0 0 0 0 0 0 1 0 0
0 0 0 0 0 0 0 1 1 0 0
0 0 0 0 0 0 0 0 1 0 0
0 0 0 0 0 0 0 1 1 0 0
0 0 0 0 0 0 0 0 1 0 0
0 0 0 0 0 0 0 1 1 0 0
0 0 0 0 0 0 0 0 1 x 0
0 0 0 0 0 0 0 1 1 1 x
0 0 0 0 0 0 0 0 1 1 x
0 0 0 0 0 0 0 1 1 1 x
*/

/* Test case 02_P02T01:
M N progIn reset progLoad start result clk valid done output
0 0 0 0 0 0 0 0 x x x
0 0 0 0 0 0 0 1 x x x
0 0 0 1 0 0 0 0 x x x
0 0 0 1 0 0 0 1 0 0 x
0 0 0 0 0 0 0 0 0 x x
0 0 0 0 0 0 0 1 0 x x
0 0 0 0 0 0 0 0 0 x x
0 0 0 0 0 0 0 1 0 x x
0 0 0 0 0 0 0 0 0 x x
0 0 0 0 0 0 0 1 0 x x
0 0 0 0 0 0 0 0 0 x x
0 0 0 0 0 0 0 1 0 x x
0 0 0 0 0 0 0 0 0 x x
0 0 0 0 0 0 0 1 0 x x
0 0 0 0 0 0 0 0 0 x x
0 0 0 0 0 0 0 1 0 x x
0 0 0 0 0 0 0 0 0 x x
0 0 0 0 0 0 0 1 0 x x
0 0 0 0 0 0 0 0 0 x x
0 0 0 0 0 0 0 1 0 x x
0 0 0 0 0 0 0 0 0 x x
0 0 0 0 0 0 0 1 0 x x
0 0 0 0 0 0 0 0 0 x x
0 0 0 0 0 0 0 1 0 x x
0 0 0 0 0 0 0 0 0 x x
0 0 0 0 0 0 0 1 0 x x
0 0 0 0 0 0 0 0 0 x x
0 0 0 0 0 0 0 1 0 x x
0 0 0 0 0 0 0 0 0 x x
0 0 0 0 0 0 0 1 0 x x
0 0 0 0 0 0 0 0 0 x x
0 0 0 0 0 0 0 1 0 x x
0 0 0 0 0 0 0 0 0 x x
0 0 0 0 0 0 0 1 0 x x
0 0 0 0 0 0 0 0 0 x x
0 0 0 0 0 0 0 1 0 x x
0 0 0 0 0 0 0 0 0 x x
0 0 0 0 0 0 0 1 0 x x
0 0 0 0 0 0 0 0 0 x x
0 0 0 0 0 0 0 1 0 x x
0 0 0 0 0 0 0 0 0 x x
0 0 0 0 0 0 0 1 0 x x
0 0 0 0 0 0 0 0 0 x x
0 0 0 0 0 0 0 1 0 x x
0 0 257 0 1 0 0 0 0 x x
0 0 257 0 1 0 0 1 0 x x
0 0 12291 0 1 0 0 0 0 x x
0 0 12291 0 1 0 0 1 0 x x
0 0 355 0 1 0 0 0 0 x x
0 0 355 0 1 0 0 1 0 x x
0 0 4352 0 1 0 0 0 0 x x
0 0 4352 0 1 0 0 1 0 x x
0 0 258 0 1 0 0 0 0 x x
0 0 258 0 1 0 0 1 0 x x
0 0 12295 0 1 0 0 0 0 x x
0 0 12295 0 1 0 0 1 0 x x
0 0 16128 0 1 0 0 0 0 x x
0 0 16128 0 1 0 0 1 0 x x
0 0 4353 0 1 0 0 0 0 x x
0 0 4353 0 1 0 0 1 0 x x
0 0 16128 0 1 0 0 0 0 x x
0 0 16128 0 1 0 0 1 0 x x
0 0 0 0 0 1 0 0 x x x
0 0 0 0 0 1 0 1 x 0 x
0 0 0 0 0 0 0 0 x 0 x
0 0 0 0 0 0 0 1 x 0 x
0 0 0 0 0 0 0 0 x 0 x
0 0 0 0 0 0 0 1 x 0 x
0 0 0 0 0 0 0 0 x 0 x
0 0 0 0 0 0 0 1 x 0 x
0 0 0 0 0 0 0 0 x 0 x
0 0 0 0 0 0 0 1 x 0 x
0 0 0 0 0 0 0 0 x 0 x
0 0 0 0 0 0 0 1 x 0 x
0 0 0 0 0 0 0 0 x 0 x
0 0 0 0 0 0 0 1 x 0 x
0 0 0 0 0 0 0 0 x 0 x
0 0 0 0 0 0 0 1 x 0 x
0 0 0 0 0 0 0 0 x 0 x
0 0 0 0 0 0 0 1 x 0 x
0 0 0 0 0 0 0 0 x 0 x
0 0 0 0 0 0 0 1 x 0 x
0 0 0 0 0 0 0 0 x 0 x
0 0 0 0 0 0 0 1 x 0 x
0 0 0 0 0 0 0 0 x 0 x
0 0 0 0 0 0 0 1 x 0 x
0 0 0 0 0 0 0 0 x 0 x
0 0 0 0 0 0 0 1 x 0 x
0 0 0 0 0 0 0 0 x 0 x
0 0 0 0 0 0 0 1 x 0 x
0 0 0 0 0 0 0 0 x 0 x
0 0 0 0 0 0 0 1 x 0 x
0 0 0 0 0 0 0 0 x 0 x
0 0 0 0 0 0 0 1 x 0 x
0 0 0 0 0 0 0 0 x 0 x
0 0 0 0 0 0 0 1 x 0 x
0 0 0 0 0 0 0 0 x 0 x
0 0 0 0 0 0 0 1 x 0 x
0 0 0 0 0 0 0 0 x 0 x
0 0 0 0 0 0 0 1 x 0 x
0 0 0 0 0 0 0 0 x 0 x
0 0 0 0 0 0 0 1 x 0 x
0 0 0 0 0 0 0 0 x 0 x
0 0 0 0 0 0 0 1 x 0 x
0 0 0 0 0 0 0 0 x 0 x
0 0 0 0 0 0 0 1 x 0 x
0 0 0 0 0 0 0 0 x 0 x
0 0 0 0 0 0 0 1 x 0 x
0 0 0 0 0 0 0 0 x 0 x
0 0 0 0 0 0 0 1 x 0 x
0 0 0 0 0 0 0 0 x 0 x
0 0 0 0 0 0 0 1 x 0 x
0 0 0 0 0 0 0 0 x 0 x
0 0 0 0 0 0 0 1 x 0 x
0 0 0 0 0 0 0 0 x 0 x
0 0 0 0 0 0 0 1 x 0 x
0 0 0 0 0 0 0 0 x 0 x
0 0 0 0 0 0 0 1 x 0 x
0 0 0 0 0 0 0 0 x 0 x
0 0 0 0 0 0 0 1 x 0 x
0 0 0 0 0 0 0 0 x 0 x
0 0 0 0 0 0 0 1 x 0 x
0 0 0 0 0 0 0 0 x 0 x
0 0 0 0 0 0 0 1 x 0 x
0 0 0 0 0 0 0 0 x 0 x
0 0 0 0 0 0 0 1 x 0 x
0 0 0 0 0 0 0 0 x 0 x
0 0 0 0 0 0 0 1 1 0 x
0 0 0 0 0 0 1 0 1 x x
0 0 0 0 0 0 1 1 1 0 1
0 0 0 0 0 0 0 0 1 0 1
0 0 0 0 0 0 0 1 1 0 2
0 0 0 0 0 0 0 0 1 0 2
0 0 0 0 0 0 0 1 1 0 0
0 0 0 0 0 0 0 0 1 0 0
0 0 0 0 0 0 0 1 1 0 0
0 0 0 0 0 0 0 0 1 0 0
0 0 0 0 0 0 0 1 1 0 0
0 0 0 0 0 0 0 0 1 0 0
0 0 0 0 0 0 0 1 1 0 0
0 0 0 0 0 0 0 0 1 0 0
0 0 0 0 0 0 0 1 1 0 0
0 0 0 0 0 0 0 0 1 0 0
0 0 0 0 0 0 0 1 1 0 0
0 0 0 0 0 0 0 0 1 0 0
0 0 0 0 0 0 0 1 1 0 0
0 0 0 0 0 0 0 0 1 0 0
0 0 0 0 0 0 0 1 1 0 0
0 0 0 0 0 0 0 0 1 0 0
0 0 0 0 0 0 0 1 1 0 0
0 0 0 0 0 0 0 0 1 0 0
0 0 0 0 0 0 0 1 1 0 0
0 0 0 0 0 0 0 0 1 0 0
0 0 0 0 0 0 0 1 1 0 0
0 0 0 0 0 0 0 0 1 0 0
0 0 0 0 0 0 0 1 1 0 0
0 0 0 0 0 0 0 0 1 0 0
0 0 0 0 0 0 0 1 1 0 0
0 0 0 0 0 0 0 0 1 0 0
0 0 0 0 0 0 0 1 1 0 0
0 0 0 0 0 0 0 0 1 x 0
0 0 0 0 0 0 0 1 1 1 x
0 0 0 0 0 0 0 0 1 1 x
0 0 0 0 0 0 0 1 1 1 x
*/

/* Test case 03_P03T01:
M N progIn reset progLoad start result clk valid done output
0 0 0 0 0 0 0 0 x x x
0 0 0 0 0 0 0 1 x x x
0 0 0 1 0 0 0 0 x x x
0 0 0 1 0 0 0 1 0 0 x
0 0 0 0 0 0 0 0 0 x x
0 0 0 0 0 0 0 1 0 x x
0 0 0 0 0 0 0 0 0 x x
0 0 0 0 0 0 0 1 0 x x
0 0 0 0 0 0 0 0 0 x x
0 0 0 0 0 0 0 1 0 x x
0 0 0 0 0 0 0 0 0 x x
0 0 0 0 0 0 0 1 0 x x
0 0 0 0 0 0 0 0 0 x x
0 0 0 0 0 0 0 1 0 x x
0 0 0 0 0 0 0 0 0 x x
0 0 0 0 0 0 0 1 0 x x
0 0 0 0 0 0 0 0 0 x x
0 0 0 0 0 0 0 1 0 x x
0 0 0 0 0 0 0 0 0 x x
0 0 0 0 0 0 0 1 0 x x
0 0 0 0 0 0 0 0 0 x x
0 0 0 0 0 0 0 1 0 x x
0 0 0 0 0 0 0 0 0 x x
0 0 0 0 0 0 0 1 0 x x
0 0 0 0 0 0 0 0 0 x x
0 0 0 0 0 0 0 1 0 x x
0 0 0 0 0 0 0 0 0 x x
0 0 0 0 0 0 0 1 0 x x
0 0 0 0 0 0 0 0 0 x x
0 0 0 0 0 0 0 1 0 x x
0 0 0 0 0 0 0 0 0 x x
0 0 0 0 0 0 0 1 0 x x
0 0 0 0 0 0 0 0 0 x x
0 0 0 0 0 0 0 1 0 x x
0 0 0 0 0 0 0 0 0 x x
0 0 0 0 0 0 0 1 0 x x
0 0 0 0 0 0 0 0 0 x x
0 0 0 0 0 0 0 1 0 x x
0 0 0 0 0 0 0 0 0 x x
0 0 0 0 0 0 0 1 0 x x
0 0 0 0 0 0 0 0 0 x x
0 0 0 0 0 0 0 1 0 x x
0 0 0 0 0 0 0 0 0 x x
0 0 0 0 0 0 0 1 0 x x
0 0 4608 0 1 0 0 0 0 x x
0 0 4608 0 1 0 0 1 0 x x
0 0 4352 0 1 0 0 0 0 x x
0 0 4352 0 1 0 0 1 0 x x
0 0 4609 0 1 0 0 0 0 x x
0 0 4609 0 1 0 0 1 0 x x
0 0 4353 0 1 0 0 0 0 x x
0 0 4353 0 1 0 0 1 0 x x
0 0 4613 0 1 0 0 0 0 x x
0 0 4613 0 1 0 0 1 0 x x
0 0 4354 0 1 0 0 0 0 x x
0 0 4354 0 1 0 0 1 0 x x
0 0 16128 0 1 0 0 0 0 x x
0 0 16128 0 1 0 0 1 0 x x
0 0 0 0 0 1 0 0 x x x
0 0 0 0 0 1 0 1 x 0 x
0 0 0 0 0 0 0 0 x 0 x
0 0 0 0 0 0 0 1 x 0 x
0 0 0 0 0 0 0 0 x 0 x
0 0 0 0 0 0 0 1 x 0 x
0 0 0 0 0 0 0 0 x 0 x
0 0 0 0 0 0 0 1 x 0 x
0 0 0 0 0 0 0 0 x 0 x
0 0 0 0 0 0 0 1 x 0 x
0 0 0 0 0 0 0 0 x 0 x
0 0 0 0 0 0 0 1 x 0 x
0 0 0 0 0 0 0 0 x 0 x
0 0 0 0 0 0 0 1 x 0 x
0 0 0 0 0 0 0 0 x 0 x
0 0 0 0 0 0 0 1 x 0 x
0 0 0 0 0 0 0 0 x 0 x
0 0 0 0 0 0 0 1 x 0 x
0 0 0 0 0 0 0 0 x 0 x
0 0 0 0 0 0 0 1 x 0 x
0 0 0 0 0 0 0 0 x 0 x
0 0 0 0 0 0 0 1 x 0 x
0 0 0 0 0 0 0 0 x 0 x
0 0 0 0 0 0 0 1 x 0 x
0 0 0 0 0 0 0 0 x 0 x
0 0 0 0 0 0 0 1 x 0 x
0 0 0 0 0 0 0 0 x 0 x
0 0 0 0 0 0 0 1 x 0 x
0 0 0 0 0 0 0 0 x 0 x
0 0 0 0 0 0 0 1 x 0 x
0 0 0 0 0 0 0 0 x 0 x
0 0 0 0 0 0 0 1 x 0 x
0 0 0 0 0 0 0 0 x 0 x
0 0 0 0 0 0 0 1 x 0 x
0 0 0 0 0 0 0 0 x 0 x
0 0 0 0 0 0 0 1 x 0 x
0 0 0 0 0 0 0 0 x 0 x
0 0 0 0 0 0 0 1 x 0 x
0 0 0 0 0 0 0 0 x 0 x
0 0 0 0 0 0 0 1 x 0 x
0 0 0 0 0 0 0 0 x 0 x
0 0 0 0 0 0 0 1 x 0 x
0 0 0 0 0 0 0 0 x 0 x
0 0 0 0 0 0 0 1 x 0 x
0 0 0 0 0 0 0 0 x 0 x
0 0 0 0 0 0 0 1 x 0 x
0 0 0 0 0 0 0 0 x 0 x
0 0 0 0 0 0 0 1 x 0 x
0 0 0 0 0 0 0 0 x 0 x
0 0 0 0 0 0 0 1 x 0 x
0 0 0 0 0 0 0 0 x 0 x
0 0 0 0 0 0 0 1 x 0 x
0 0 0 0 0 0 0 0 x 0 x
0 0 0 0 0 0 0 1 x 0 x
0 0 0 0 0 0 0 0 x 0 x
0 0 0 0 0 0 0 1 x 0 x
0 0 0 0 0 0 0 0 x 0 x
0 0 0 0 0 0 0 1 x 0 x
0 0 0 0 0 0 0 0 x 0 x
0 0 0 0 0 0 0 1 x 0 x
0 0 0 0 0 0 0 0 x 0 x
0 0 0 0 0 0 0 1 x 0 x
0 0 0 0 0 0 0 0 x 0 x
0 0 0 0 0 0 0 1 x 0 x
0 0 0 0 0 0 0 0 x 0 x
0 0 0 0 0 0 0 1 1 0 x
0 0 0 0 0 0 1 0 1 x x
0 0 0 0 0 0 1 1 1 0 0
0 0 0 0 0 0 0 0 1 0 0
0 0 0 0 0 0 0 1 1 0 0
0 0 0 0 0 0 0 0 1 0 0
0 0 0 0 0 0 0 1 1 0 2
0 0 0 0 0 0 0 0 1 0 2
0 0 0 0 0 0 0 1 1 0 0
0 0 0 0 0 0 0 0 1 0 0
0 0 0 0 0 0 0 1 1 0 0
0 0 0 0 0 0 0 0 1 0 0
0 0 0 0 0 0 0 1 1 0 0
0 0 0 0 0 0 0 0 1 0 0
0 0 0 0 0 0 0 1 1 0 0
0 0 0 0 0 0 0 0 1 0 0
0 0 0 0 0 0 0 1 1 0 0
0 0 0 0 0 0 0 0 1 0 0
0 0 0 0 0 0 0 1 1 0 0
0 0 0 0 0 0 0 0 1 0 0
0 0 0 0 0 0 0 1 1 0 0
0 0 0 0 0 0 0 0 1 0 0
0 0 0 0 0 0 0 1 1 0 0
0 0 0 0 0 0 0 0 1 0 0
0 0 0 0 0 0 0 1 1 0 0
0 0 0 0 0 0 0 0 1 0 0
0 0 0 0 0 0 0 1 1 0 0
0 0 0 0 0 0 0 0 1 0 0
0 0 0 0 0 0 0 1 1 0 0
0 0 0 0 0 0 0 0 1 0 0
0 0 0 0 0 0 0 1 1 0 0
0 0 0 0 0 0 0 0 1 0 0
0 0 0 0 0 0 0 1 1 0 0
0 0 0 0 0 0 0 0 1 x 0
0 0 0 0 0 0 0 1 1 1 x
0 0 0 0 0 0 0 0 1 1 x
0 0 0 0 0 0 0 1 1 1 x
*/

/* Test case 04_P04T01:
M N progIn reset progLoad start result clk valid done output
0 0 0 0 0 0 0 0 x x x
0 0 0 0 0 0 0 1 x x x
0 0 0 1 0 0 0 0 x x x
0 0 0 1 0 0 0 1 0 0 x
0 0 0 0 0 0 0 0 0 x x
0 0 0 0 0 0 0 1 0 x x
0 0 0 0 0 0 0 0 0 x x
0 0 0 0 0 0 0 1 0 x x
0 0 0 0 0 0 0 0 0 x x
0 0 0 0 0 0 0 1 0 x x
0 0 0 0 0 0 0 0 0 x x
0 0 0 0 0 0 0 1 0 x x
0 0 0 0 0 0 0 0 0 x x
0 0 0 0 0 0 0 1 0 x x
0 0 0 0 0 0 0 0 0 x x
0 0 0 0 0 0 0 1 0 x x
0 0 0 0 0 0 0 0 0 x x
0 0 0 0 0 0 0 1 0 x x
0 0 0 0 0 0 0 0 0 x x
0 0 0 0 0 0 0 1 0 x x
0 0 0 0 0 0 0 0 0 x x
0 0 0 0 0 0 0 1 0 x x
0 0 0 0 0 0 0 0 0 x x
0 0 0 0 0 0 0 1 0 x x
0 0 0 0 0 0 0 0 0 x x
0 0 0 0 0 0 0 1 0 x x
0 0 0 0 0 0 0 0 0 x x
0 0 0 0 0 0 0 1 0 x x
0 0 0 0 0 0 0 0 0 x x
0 0 0 0 0 0 0 1 0 x x
0 0 0 0 0 0 0 0 0 x x
0 0 0 0 0 0 0 1 0 x x
0 0 0 0 0 0 0 0 0 x x
0 0 0 0 0 0 0 1 0 x x
0 0 0 0 0 0 0 0 0 x x
0 0 0 0 0 0 0 1 0 x x
0 0 0 0 0 0 0 0 0 x x
0 0 0 0 0 0 0 1 0 x x
0 0 0 0 0 0 0 0 0 x x
0 0 0 0 0 0 0 1 0 x x
0 0 0 0 0 0 0 0 0 x x
0 0 0 0 0 0 0 1 0 x x
0 0 0 0 0 0 0 0 0 x x
0 0 0 0 0 0 0 1 0 x x
0 0 263 0 1 0 0 0 0 x x
0 0 263 0 1 0 0 1 0 x x
0 0 14592 0 1 0 0 0 0 x x
0 0 14592 0 1 0 0 1 0 x x
0 0 256 0 1 0 0 0 0 x x
0 0 256 0 1 0 0 1 0 x x
0 0 12549 0 1 0 0 0 0 x x
0 0 12549 0 1 0 0 1 0 x x
0 0 12294 0 1 0 0 0 0 x x
0 0 12294 0 1 0 0 1 0 x x
0 0 257 0 1 0 0 0 0 x x
0 0 257 0 1 0 0 1 0 x x
0 0 4352 0 1 0 0 0 0 x x
0 0 4352 0 1 0 0 1 0 x x
0 0 265 0 1 0 0 0 0 x x
0 0 265 0 1 0 0 1 0 x x
0 0 14592 0 1 0 0 0 0 x x
0 0 14592 0 1 0 0 1 0 x x
0 0 256 0 1 0 0 0 0 x x
0 0 256 0 1 0 0 1 0 x x
0 0 12556 0 1 0 0 0 0 x x
0 0 12556 0 1 0 0 1 0 x x
0 0 12301 0 1 0 0 0 0 x x
0 0 12301 0 1 0 0 1 0 x x
0 0 257 0 1 0 0 0 0 x x
0 0 257 0 1 0 0 1 0 x x
0 0 4353 0 1 0 0 0 0 x x
0 0 4353 0 1 0 0 1 0 x x
0 0 269 0 1 0 0 0 0 x x
0 0 269 0 1 0 0 1 0 x x
0 0 14592 0 1 0 0 0 0 x x
0 0 14592 0 1 0 0 1 0 x x
0 0 256 0 1 0 0 0 0 x x
0 0 256 0 1 0 0 1 0 x x
0 0 12563 0 1 0 0 0 0 x x
0 0 12563 0 1 0 0 1 0 x x
0 0 12308 0 1 0 0 0 0 x x
0 0 12308 0 1 0 0 1 0 x x
0 0 257 0 1 0 0 0 0 x x
0 0 257 0 1 0 0 1 0 x x
0 0 4354 0 1 0 0 0 0 x x
0 0 4354 0 1 0 0 1 0 x x
0 0 271 0 1 0 0 0 0 x x
0 0 271 0 1 0 0 1 0 x x
0 0 14592 0 1 0 0 0 0 x x
0 0 14592 0 1 0 0 1 0 x x
0 0 256 0 1 0 0 0 0 x x
0 0 256 0 1 0 0 1 0 x x
0 0 12570 0 1 0 0 0 0 x x
0 0 12570 0 1 0 0 1 0 x x
0 0 12315 0 1 0 0 0 0 x x
0 0 12315 0 1 0 0 1 0 x x
0 0 257 0 1 0 0 0 0 x x
0 0 257 0 1 0 0 1 0 x x
0 0 4355 0 1 0 0 0 0 x x
0 0 4355 0 1 0 0 1 0 x x
0 0 273 0 1 0 0 0 0 x x
0 0 273 0 1 0 0 1 0 x x
0 0 14592 0 1 0 0 0 0 x x
0 0 14592 0 1 0 0 1 0 x x
0 0 256 0 1 0 0 0 0 x x
0 0 256 0 1 0 0 1 0 x x
0 0 12577 0 1 0 0 0 0 x x
0 0 12577 0 1 0 0 1 0 x x
0 0 12322 0 1 0 0 0 0 x x
0 0 12322 0 1 0 0 1 0 x x
0 0 257 0 1 0 0 0 0 x x
0 0 257 0 1 0 0 1 0 x x
0 0 4356 0 1 0 0 0 0 x x
0 0 4356 0 1 0 0 1 0 x x
0 0 277 0 1 0 0 0 0 x x
0 0 277 0 1 0 0 1 0 x x
0 0 14592 0 1 0 0 0 0 x x
0 0 14592 0 1 0 0 1 0 x x
0 0 256 0 1 0 0 0 0 x x
0 0 256 0 1 0 0 1 0 x x
0 0 12584 0 1 0 0 0 0 x x
0 0 12584 0 1 0 0 1 0 x x
0 0 12329 0 1 0 0 0 0 x x
0 0 12329 0 1 0 0 1 0 x x
0 0 257 0 1 0 0 0 0 x x
0 0 257 0 1 0 0 1 0 x x
0 0 4357 0 1 0 0 0 0 x x
0 0 4357 0 1 0 0 1 0 x x
0 0 279 0 1 0 0 0 0 x x
0 0 279 0 1 0 0 1 0 x x
0 0 14592 0 1 0 0 0 0 x x
0 0 14592 0 1 0 0 1 0 x x
0 0 256 0 1 0 0 0 0 x x
0 0 256 0 1 0 0 1 0 x x
0 0 12591 0 1 0 0 0 0 x x
0 0 12591 0 1 0 0 1 0 x x
0 0 12336 0 1 0 0 0 0 x x
0 0 12336 0 1 0 0 1 0 x x
0 0 257 0 1 0 0 0 0 x x
0 0 257 0 1 0 0 1 0 x x
0 0 4358 0 1 0 0 0 0 x x
0 0 4358 0 1 0 0 1 0 x x
0 0 281 0 1 0 0 0 0 x x
0 0 281 0 1 0 0 1 0 x x
0 0 14592 0 1 0 0 0 0 x x
0 0 14592 0 1 0 0 1 0 x x
0 0 256 0 1 0 0 0 0 x x
0 0 256 0 1 0 0 1 0 x x
0 0 12598 0 1 0 0 0 0 x x
0 0 12598 0 1 0 0 1 0 x x
0 0 12343 0 1 0 0 0 0 x x
0 0 12343 0 1 0 0 1 0 x x
0 0 257 0 1 0 0 0 0 x x
0 0 257 0 1 0 0 1 0 x x
0 0 4359 0 1 0 0 0 0 x x
0 0 4359 0 1 0 0 1 0 x x
0 0 16128 0 1 0 0 0 0 x x
0 0 16128 0 1 0 0 1 0 x x
0 0 0 0 0 1 0 0 x x x
0 0 0 0 0 1 0 1 x 0 x
0 0 0 0 0 0 0 0 x 0 x
0 0 0 0 0 0 0 1 x 0 x
0 0 0 0 0 0 0 0 x 0 x
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*/

/* Test case 05_P05T01:
M N progIn reset progLoad start result clk valid done output
0 0 0 0 0 0 0 0 x x x
0 0 0 0 0 0 0 1 x x x
0 0 0 1 0 0 0 0 x x x
0 0 0 1 0 0 0 1 0 0 x
0 0 0 0 0 0 0 0 0 x x
0 0 0 0 0 0 0 1 0 x x
0 0 0 0 0 0 0 0 0 x x
0 0 0 0 0 0 0 1 0 x x
0 0 0 0 0 0 0 0 0 x x
0 0 0 0 0 0 0 1 0 x x
0 0 0 0 0 0 0 0 0 x x
0 0 0 0 0 0 0 1 0 x x
0 0 0 0 0 0 0 0 0 x x
0 0 0 0 0 0 0 1 0 x x
0 0 0 0 0 0 0 0 0 x x
0 0 0 0 0 0 0 1 0 x x
0 0 0 0 0 0 0 0 0 x x
0 0 0 0 0 0 0 1 0 x x
0 0 0 0 0 0 0 0 0 x x
0 0 0 0 0 0 0 1 0 x x
0 0 0 0 0 0 0 0 0 x x
0 0 0 0 0 0 0 1 0 x x
0 0 0 0 0 0 0 0 0 x x
0 0 0 0 0 0 0 1 0 x x
0 0 0 0 0 0 0 0 0 x x
0 0 0 0 0 0 0 1 0 x x
0 0 0 0 0 0 0 0 0 x x
0 0 0 0 0 0 0 1 0 x x
0 0 0 0 0 0 0 0 0 x x
0 0 0 0 0 0 0 1 0 x x
0 0 0 0 0 0 0 0 0 x x
0 0 0 0 0 0 0 1 0 x x
0 0 0 0 0 0 0 0 0 x x
0 0 0 0 0 0 0 1 0 x x
0 0 0 0 0 0 0 0 0 x x
0 0 0 0 0 0 0 1 0 x x
0 0 0 0 0 0 0 0 0 x x
0 0 0 0 0 0 0 1 0 x x
0 0 0 0 0 0 0 0 0 x x
0 0 0 0 0 0 0 1 0 x x
0 0 0 0 0 0 0 0 0 x x
0 0 0 0 0 0 0 1 0 x x
0 0 0 0 0 0 0 0 0 x x
0 0 0 0 0 0 0 1 0 x x
0 0 265 0 1 0 0 0 0 x x
0 0 265 0 1 0 0 1 0 x x
0 0 515 0 1 0 0 0 0 x x
0 0 515 0 1 0 0 1 0 x x
0 0 14336 0 1 0 0 0 0 x x
0 0 14336 0 1 0 0 1 0 x x
0 0 14592 0 1 0 0 0 0 x x
0 0 14592 0 1 0 0 1 0 x x
0 0 12562 0 1 0 0 0 0 x x
0 0 12562 0 1 0 0 1 0 x x
0 0 12807 0 1 0 0 0 0 x x
0 0 12807 0 1 0 0 1 0 x x
0 0 12306 0 1 0 0 0 0 x x
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*/

/* Test case 06_P06T01:
M N progIn reset progLoad start result clk valid done output
0 0 0 0 0 0 0 0 x x x
0 0 0 0 0 0 0 1 x x x
0 0 0 1 0 0 0 0 x x x
0 0 0 1 0 0 0 1 0 0 x
0 0 0 0 0 0 0 0 0 x x
0 0 0 0 0 0 0 1 0 x x
0 0 0 0 0 0 0 0 0 x x
0 0 0 0 0 0 0 1 0 x x
0 0 0 0 0 0 0 0 0 x x
0 0 0 0 0 0 0 1 0 x x
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*/

/* Test case 07_P07T01:
M N progIn reset progLoad start result clk valid done output
0 0 0 0 0 0 0 0 x x x
0 0 0 0 0 0 0 1 x x x
0 0 0 1 0 0 0 0 x x x
0 0 0 1 0 0 0 1 0 0 x
0 0 0 0 0 0 0 0 0 x x
0 0 0 0 0 0 0 1 0 x x
0 0 0 0 0 0 0 0 0 x x
0 0 0 0 0 0 0 1 0 x x
0 0 0 0 0 0 0 0 0 x x
0 0 0 0 0 0 0 1 0 x x
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*/

/* Test case 08_P08T01:
M N progIn reset progLoad start result clk valid done output
0 0 0 0 0 0 0 0 x x x
0 0 0 0 0 0 0 1 x x x
0 0 0 1 0 0 0 0 x x x
0 0 0 1 0 0 0 1 0 0 x
0 0 0 0 0 0 0 0 0 x x
0 0 0 0 0 0 0 1 0 x x
0 0 0 0 0 0 0 0 0 x x
0 0 0 0 0 0 0 1 0 x x
0 0 0 0 0 0 0 0 0 x x
0 0 0 0 0 0 0 1 0 x x
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*/

/* Test case 09_P09T01:
M N progIn reset progLoad start result clk valid done output
0 0 0 0 0 0 0 0 x x x
0 0 0 0 0 0 0 1 x x x
0 0 0 1 0 0 0 0 x x x
0 0 0 1 0 0 0 1 0 0 x
0 0 0 0 0 0 0 0 0 x x
0 0 0 0 0 0 0 1 0 x x
0 0 0 0 0 0 0 0 0 x x
0 0 0 0 0 0 0 1 0 x x
0 0 0 0 0 0 0 0 0 x x
0 0 0 0 0 0 0 1 0 x x
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*/

/* Test case 10_P10T01:
M N progIn reset progLoad start result clk valid done output
0 0 0 0 0 0 0 0 x x x
0 0 0 0 0 0 0 1 x x x
0 0 0 1 0 0 0 0 x x x
0 0 0 1 0 0 0 1 0 0 x
0 0 0 0 0 0 0 0 0 x x
0 0 0 0 0 0 0 1 0 x x
0 0 0 0 0 0 0 0 0 x x
0 0 0 0 0 0 0 1 0 x x
0 0 0 0 0 0 0 0 0 x x
0 0 0 0 0 0 0 1 0 x x
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*/

/* Test case 11_P11T01:
M N progIn reset progLoad start result clk valid done output
0 0 0 0 0 0 0 0 x x x
0 0 0 0 0 0 0 1 x x x
0 0 0 1 0 0 0 0 x x x
0 0 0 1 0 0 0 1 0 0 x
0 0 0 0 0 0 0 0 0 x x
0 0 0 0 0 0 0 1 0 x x
0 0 0 0 0 0 0 0 0 x x
0 0 0 0 0 0 0 1 0 x x
0 0 0 0 0 0 0 0 0 x x
0 0 0 0 0 0 0 1 0 x x
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*/

/* Test case 12_P12T01:
M N progIn reset progLoad start result clk valid done output
0 0 0 0 0 0 0 0 x x x
0 0 0 0 0 0 0 1 x x x
0 0 0 1 0 0 0 0 x x x
0 0 0 1 0 0 0 1 0 0 x
0 0 0 0 0 0 0 0 0 x x
0 0 0 0 0 0 0 1 0 x x
0 0 0 0 0 0 0 0 0 x x
0 0 0 0 0 0 0 1 0 x x
0 0 0 0 0 0 0 0 0 x x
0 0 0 0 0 0 0 1 0 x x
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*/

/* Test case 13_P13T01:
M N progIn reset progLoad start result clk valid done output
0 0 0 0 0 0 0 0 x x x
0 0 0 0 0 0 0 1 x x x
0 0 0 1 0 0 0 0 x x x
0 0 0 1 0 0 0 1 0 0 x
0 0 0 0 0 0 0 0 0 x x
0 0 0 0 0 0 0 1 0 x x
0 0 0 0 0 0 0 0 0 x x
0 0 0 0 0 0 0 1 0 x x
0 0 0 0 0 0 0 0 0 x x
0 0 0 0 0 0 0 1 0 x x
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*/
